// Logisim project Anzeige_7Segment.circ as structural Verilog: 14 circuits, main circuit Hauptschaltung_7Seg_Anzeige
module Hauptschaltung_7Seg_Anzeige (
  input  Takt_Wecker_Stellen,
  input  Taste_Gecko_Min_Sek,
  input  Taste_Gecko_Tag_Mon,
  input  Taste_Gecko_Jahr,
  input  Schalter_Gecko_Wecker_Stellem,
  input  [4:0] Tagbits,
  input  [4:0] Stundenbits,
  input  [4:0] Wecker_Stundenbits,
  input  [3:0] Monatbits,
  input  [5:0] Minutenbits,
  input  [5:0] Wecker_Minutenbits,
  input  [6:0] Jahrbits,
  input  [5:0] Sekundenbits,
  input  Schalter_Gecko_Wecker_Ein_Aus,
  output Seg_1A,
  output Seg_1B,
  output Seg_1C,
  output Seg_1D,
  output Seg_1E,
  output Seg_1F,
  output Seg_1G,
  output Seg_2A,
  output Seg_2B,
  output Seg_2C,
  output Seg_2D,
  output Seg_2E,
  output Seg_2F,
  output Seg_2G,
  output Seg_3A,
  output Seg_3B,
  output Seg_3C,
  output Seg_3D,
  output Seg_3E,
  output Seg_3F,
  output Seg_3G,
  output Seg_4A,
  output Seg_4B,
  output Seg_4C,
  output Seg_4D,
  output Seg_4E,
  output Seg_4F,
  output Seg_4G,
  output Weckerfunktion_zu_LED,
  output Min_sek_zu_LED,
  output Tag_Mon_zu_LED,
  output Jahr_zu_LED
);

  wire bcd2_7seg_1_seg_a, bcd2_7seg_1_seg_b, bcd2_7seg_1_seg_c, bcd2_7seg_1_seg_d, bcd2_7seg_1_seg_e,
       bcd2_7seg_1_seg_f, bcd2_7seg_1_seg_g, bcd2_7seg_2_seg_a, bcd2_7seg_2_seg_b, bcd2_7seg_2_seg_c,
       bcd2_7seg_2_seg_d, bcd2_7seg_2_seg_e, bcd2_7seg_2_seg_f, bcd2_7seg_2_seg_g, bcd2_7seg_3_seg_a,
       bcd2_7seg_3_seg_b, bcd2_7seg_3_seg_c, bcd2_7seg_3_seg_d, bcd2_7seg_3_seg_e, bcd2_7seg_3_seg_f,
       bcd2_7seg_3_seg_g, bcd2_7seg_4_seg_a, bcd2_7seg_4_seg_b, bcd2_7seg_4_seg_c, bcd2_7seg_4_seg_d,
       bcd2_7seg_4_seg_e, bcd2_7seg_4_seg_f, bcd2_7seg_4_seg_g, bin2_bcd_1_d_0, bin2_bcd_1_d_1,
       bin2_bcd_1_d_2, bin2_bcd_1_d_3, bin2_bcd_1_u_0, bin2_bcd_1_u_1, bin2_bcd_1_u_2, bin2_bcd_1_u_3,
       bin2_bcd_2_d_0, bin2_bcd_2_d_1, bin2_bcd_2_d_2, bin2_bcd_2_d_3, bin2_bcd_2_u_0, bin2_bcd_2_u_1,
       bin2_bcd_2_u_2, bin2_bcd_2_u_3, multiplex_jahr_sekunden_1_bit0, multiplex_jahr_sekunden_1_bit1,
       multiplex_jahr_sekunden_1_bit2, multiplex_jahr_sekunden_1_bit3, multiplex_jahr_sekunden_1_bit4,
       multiplex_jahr_sekunden_1_bit5, multiplex_jahr_sekunden_1_bit6, multiplex_min_monat_1_bit0,
       multiplex_min_monat_1_bit1, multiplex_min_monat_1_bit2, multiplex_min_monat_1_bit3,
       multiplex_min_monat_1_bit4, multiplex_min_monat_1_bit5, multiplex_std_tag_1_bit0,
       multiplex_std_tag_1_bit1, multiplex_std_tag_1_bit2, multiplex_std_tag_1_bit3,
       multiplex_std_tag_1_bit4, tastenfehler_1_wecker_stellen, umschaltung_min_1_seg1_bit_0,
       umschaltung_min_1_seg1_bit_1, umschaltung_min_1_seg1_bit_2, umschaltung_min_1_seg1_bit_3,
       umschaltung_min_1_seg1_bit_4, umschaltung_min_1_seg1_bit_5, umschaltung_min_1_seg2_bit_0,
       umschaltung_min_1_seg2_bit_1, umschaltung_min_1_seg2_bit_2, umschaltung_min_1_seg2_bit_3,
       umschaltung_min_1_seg2_bit_4, umschaltung_min_1_seg2_bit_5, verknuepfung_min_mon_jahr_1_out_13,
       verknuepfung_min_mon_jahr_1_out_14, verknuepfung_min_mon_jahr_1_out_15,
       verknuepfung_min_mon_jahr_1_out_16, verknuepfung_min_mon_jahr_1_out_17,
       verknuepfung_min_mon_jahr_1_out_18, verknuepfung_min_mon_jahr_2_out_13,
       verknuepfung_min_mon_jahr_2_out_14, verknuepfung_min_mon_jahr_2_out_15,
       verknuepfung_min_mon_jahr_2_out_16, verknuepfung_min_mon_jahr_2_out_17,
       verknuepfung_min_mon_jahr_2_out_18;

  Tastenfehler tastenfehler_1 (
    .Taste_Gecko_Min_Sek(Taste_Gecko_Min_Sek), .Taste_Gecko_Tag_Mon(Taste_Gecko_Tag_Mon),
    .Taste_Gecko_Jahr(Taste_Gecko_Jahr), .Schalter_Gecko_Wecker_Stellen(Schalter_Gecko_Wecker_Stellem),
    .Taste_Min_Sek(Min_sek_zu_LED), .Taste_Tag_Mon(Tag_Mon_zu_LED), .Taste_Jahr(Jahr_zu_LED),
    .Wecker_Stellen(tastenfehler_1_wecker_stellen));
  Multiplex_Std_Tag multiplex_std_tag_1 (
    .Eingangstaste_Min_Sek(Min_sek_zu_LED), .Eingangstaste_Tag_Monat(Tag_Mon_zu_LED),
    .Eingangstaste_Jahr(Jahr_zu_LED), .Wecker_Stellen(tastenfehler_1_wecker_stellen), .Tag_Bit0(Tagbits[0]),
    .Tag_Bit1(Tagbits[1]), .Tag_Bit2(Tagbits[2]), .Tag_Bit3(Tagbits[3]), .Tag_Bit4(Tagbits[4]),
    .Std_Bit0(Stundenbits[0]), .Std_Bit1(Stundenbits[1]), .Std_Bit2(Stundenbits[2]),
    .Std_Bit3(Stundenbits[3]), .Std_Bit4(Stundenbits[4]), .Wecker_Std_Bit_0(Wecker_Stundenbits[0]),
    .Wecker_Std_Bit_1(Wecker_Stundenbits[1]), .Wecker_Std_Bit_2(Wecker_Stundenbits[2]),
    .Wecker_Std_Bit_3(Wecker_Stundenbits[3]), .Wecker_Std_Bit_4(Wecker_Stundenbits[4]),
    .Bit0(multiplex_std_tag_1_bit0), .Bit1(multiplex_std_tag_1_bit1), .Bit2(multiplex_std_tag_1_bit2),
    .Bit3(multiplex_std_tag_1_bit3), .Bit4(multiplex_std_tag_1_bit4));
  Multiplex_Min_Monat multiplex_min_monat_1 (
    .Eingangstaste_Tag_Monat(Tag_Mon_zu_LED), .Eingangstaste_Jahr(Jahr_zu_LED),
    .Wecker_Stellen(tastenfehler_1_wecker_stellen), .Monat_Bit0(Monatbits[0]), .Monat_Bit1(Monatbits[1]),
    .Monat_Bit2(Monatbits[2]), .Monat_Bit3(Monatbits[3]), .Min_Bit0(Minutenbits[0]),
    .Min_Bit1(Minutenbits[1]), .Min_Bit2(Minutenbits[2]), .Min_Bit3(Minutenbits[3]),
    .Min_Bit4(Minutenbits[4]), .Min_Bit5(Minutenbits[5]), .Wecker_Min_Bit_0(Wecker_Minutenbits[0]),
    .Wecker_Min_Bit_1(Wecker_Minutenbits[1]), .Wecker_Min_Bit_2(Wecker_Minutenbits[2]),
    .Wecker_Min_Bit_3(Wecker_Minutenbits[3]), .Wecker_Min_Bit_4(Wecker_Minutenbits[4]),
    .Wecker_Min_Bit_5(Wecker_Minutenbits[5]), .Bit0(multiplex_min_monat_1_bit0),
    .Bit1(multiplex_min_monat_1_bit1), .Bit2(multiplex_min_monat_1_bit2), .Bit3(multiplex_min_monat_1_bit3),
    .Bit4(multiplex_min_monat_1_bit4), .Bit5(multiplex_min_monat_1_bit5));
  Multiplex_Jahr_Sekunden multiplex_jahr_sekunden_1 (
    .Eingangstaste_Jahr(Jahr_zu_LED), .Eingangstaste_Min_Sek(Min_sek_zu_LED), .Jahr_Bit0(Jahrbits[0]),
    .Jahr_Bit1(Jahrbits[1]), .Jahr_Bit2(Jahrbits[2]), .Jahr_Bit3(Jahrbits[3]), .Jahr_Bit4(Jahrbits[4]),
    .Jahr_Bit5(Jahrbits[5]), .Jahr_Bit6(Jahrbits[6]), .Sekunden_Bit_0(Sekundenbits[0]),
    .Sekunden_Bit_1(Sekundenbits[1]), .Sekunden_Bit_2(Sekundenbits[2]), .Sekunden_Bit_3(Sekundenbits[3]),
    .Sekunden_Bit_4(Sekundenbits[4]), .Sekunden_Bit_5(Sekundenbits[5]),
    .Bit0(multiplex_jahr_sekunden_1_bit0), .Bit1(multiplex_jahr_sekunden_1_bit1),
    .Bit2(multiplex_jahr_sekunden_1_bit2), .Bit3(multiplex_jahr_sekunden_1_bit3),
    .Bit4(multiplex_jahr_sekunden_1_bit4), .Bit5(multiplex_jahr_sekunden_1_bit5),
    .Bit6(multiplex_jahr_sekunden_1_bit6));
  Weckfunktion_Zeitvergleich weckfunktion_zeitvergleich_1 (
    .Wecker_Ein_Aus(Schalter_Gecko_Wecker_Ein_Aus), .Stunde_Aktuell_0(Stundenbits[0]),
    .Stunde_Aktuell_1(Stundenbits[1]), .Stunde_Aktuell_2(Stundenbits[2]), .Stunde_Aktuell_3(Stundenbits[3]),
    .Stunde_Aktuell_4(Stundenbits[4]), .Stunde_Wecker_0(Wecker_Stundenbits[0]),
    .Stunde_Wecker_1(Wecker_Stundenbits[1]), .Stunde_Wecker_2(Wecker_Stundenbits[2]),
    .Stunde_Wecker_3(Wecker_Stundenbits[3]), .Stunde_Wecker_4(Wecker_Stundenbits[4]),
    .MInute_Aktuell_0(Minutenbits[0]), .MInute_Aktuell_1(Minutenbits[1]), .MInute_Aktuell_2(Minutenbits[2]),
    .MInute_Aktuell_3(Minutenbits[3]), .MInute_Aktuell_4(Minutenbits[4]), .MInute_Aktuell_5(Minutenbits[5]),
    .MInute_Wecker_0(Wecker_Minutenbits[0]), .MInute_Wecker_1(Wecker_Minutenbits[1]),
    .MInute_Wecker_2(Wecker_Minutenbits[2]), .MInute_Wecker_3(Wecker_Minutenbits[3]),
    .MInute_Wecker_4(Wecker_Minutenbits[4]), .MInute_Wecker_5(Wecker_Minutenbits[5]),
    .Nach_LED_Anzeige_Weckfunktion(Weckerfunktion_zu_LED));
  Umschaltung_Min umschaltung_min_1 (
    .Taste_Min_Sek(Min_sek_zu_LED), .Bit_0(multiplex_min_monat_1_bit0), .Bit_1(multiplex_min_monat_1_bit1),
    .Bit_2(multiplex_min_monat_1_bit2), .Bit_3(multiplex_min_monat_1_bit3),
    .Bit_4(multiplex_min_monat_1_bit4), .Bit_5(multiplex_min_monat_1_bit5),
    .Seg1_Bit_0(umschaltung_min_1_seg1_bit_0), .Seg1_Bit_1(umschaltung_min_1_seg1_bit_1),
    .Seg1_Bit_2(umschaltung_min_1_seg1_bit_2), .Seg1_Bit_3(umschaltung_min_1_seg1_bit_3),
    .Seg1_Bit_4(umschaltung_min_1_seg1_bit_4), .Seg1_Bit_5(umschaltung_min_1_seg1_bit_5),
    .Seg2_Bit_0(umschaltung_min_1_seg2_bit_0), .Seg2_Bit_1(umschaltung_min_1_seg2_bit_1),
    .Seg2_Bit_2(umschaltung_min_1_seg2_bit_2), .Seg2_Bit_3(umschaltung_min_1_seg2_bit_3),
    .Seg2_Bit_4(umschaltung_min_1_seg2_bit_4), .Seg2_Bit_5(umschaltung_min_1_seg2_bit_5));
  Verknuepfung_min_mon_jahr verknuepfung_min_mon_jahr_1 (
    .in_1(multiplex_std_tag_1_bit0), .in_2(umschaltung_min_1_seg1_bit_0), .in_3(multiplex_std_tag_1_bit1),
    .in_4(umschaltung_min_1_seg1_bit_1), .in_5(multiplex_std_tag_1_bit2),
    .in_6(umschaltung_min_1_seg1_bit_2), .in_7(multiplex_std_tag_1_bit3),
    .in_8(umschaltung_min_1_seg1_bit_3), .in_9(multiplex_std_tag_1_bit4),
    .in_10(umschaltung_min_1_seg1_bit_4), .in_12(umschaltung_min_1_seg1_bit_5),
    .out_13(verknuepfung_min_mon_jahr_1_out_13), .out_14(verknuepfung_min_mon_jahr_1_out_14),
    .out_15(verknuepfung_min_mon_jahr_1_out_15), .out_16(verknuepfung_min_mon_jahr_1_out_16),
    .out_17(verknuepfung_min_mon_jahr_1_out_17), .out_18(verknuepfung_min_mon_jahr_1_out_18));  // open: in_11
  Bin2_BCD bin2_bcd_1 (
    .A_0(verknuepfung_min_mon_jahr_1_out_13), .A_1(verknuepfung_min_mon_jahr_1_out_14),
    .A_2(verknuepfung_min_mon_jahr_1_out_15), .A_3(verknuepfung_min_mon_jahr_1_out_16),
    .A_4(verknuepfung_min_mon_jahr_1_out_17), .A_5(verknuepfung_min_mon_jahr_1_out_18), .D_0(bin2_bcd_1_d_0),
    .D_1(bin2_bcd_1_d_1), .D_2(bin2_bcd_1_d_2), .D_3(bin2_bcd_1_d_3), .U_0(bin2_bcd_1_u_0),
    .U_1(bin2_bcd_1_u_1), .U_2(bin2_bcd_1_u_2), .U_3(bin2_bcd_1_u_3));  // open: A_6, A_7, A_8, C_0, C_1, C_2
  Verknuepfung_min_mon_jahr verknuepfung_min_mon_jahr_2 (
    .in_1(umschaltung_min_1_seg2_bit_0), .in_2(multiplex_jahr_sekunden_1_bit0),
    .in_3(umschaltung_min_1_seg2_bit_1), .in_4(multiplex_jahr_sekunden_1_bit1),
    .in_5(umschaltung_min_1_seg2_bit_2), .in_6(multiplex_jahr_sekunden_1_bit2),
    .in_7(umschaltung_min_1_seg2_bit_3), .in_8(multiplex_jahr_sekunden_1_bit3),
    .in_9(umschaltung_min_1_seg2_bit_4), .in_10(multiplex_jahr_sekunden_1_bit4),
    .in_11(umschaltung_min_1_seg2_bit_5), .in_12(multiplex_jahr_sekunden_1_bit5),
    .out_13(verknuepfung_min_mon_jahr_2_out_13), .out_14(verknuepfung_min_mon_jahr_2_out_14),
    .out_15(verknuepfung_min_mon_jahr_2_out_15), .out_16(verknuepfung_min_mon_jahr_2_out_16),
    .out_17(verknuepfung_min_mon_jahr_2_out_17), .out_18(verknuepfung_min_mon_jahr_2_out_18));
  Bin2_BCD bin2_bcd_2 (
    .A_0(verknuepfung_min_mon_jahr_2_out_13), .A_1(verknuepfung_min_mon_jahr_2_out_14),
    .A_2(verknuepfung_min_mon_jahr_2_out_15), .A_3(verknuepfung_min_mon_jahr_2_out_16),
    .A_4(verknuepfung_min_mon_jahr_2_out_17), .A_5(verknuepfung_min_mon_jahr_2_out_18),
    .A_6(multiplex_jahr_sekunden_1_bit6), .D_0(bin2_bcd_2_d_0), .D_1(bin2_bcd_2_d_1), .D_2(bin2_bcd_2_d_2),
    .D_3(bin2_bcd_2_d_3), .U_0(bin2_bcd_2_u_0), .U_1(bin2_bcd_2_u_1), .U_2(bin2_bcd_2_u_2),
    .U_3(bin2_bcd_2_u_3));  // open: A_7, A_8, C_0, C_1, C_2
  BCD2_7Seg bcd2_7seg_1 (
    .A0(bin2_bcd_1_d_0), .A1(bin2_bcd_1_d_1), .A2(bin2_bcd_1_d_2), .A3(bin2_bcd_1_d_3),
    .Seg_A(bcd2_7seg_1_seg_a), .Seg_B(bcd2_7seg_1_seg_b), .Seg_C(bcd2_7seg_1_seg_c),
    .Seg_D(bcd2_7seg_1_seg_d), .Seg_E(bcd2_7seg_1_seg_e), .Seg_F(bcd2_7seg_1_seg_f), .Seg_G(bcd2_7seg_1_seg_g));
  BCD2_7Seg bcd2_7seg_2 (
    .A0(bin2_bcd_1_u_0), .A1(bin2_bcd_1_u_1), .A2(bin2_bcd_1_u_2), .A3(bin2_bcd_1_u_3),
    .Seg_A(bcd2_7seg_2_seg_a), .Seg_B(bcd2_7seg_2_seg_b), .Seg_C(bcd2_7seg_2_seg_c),
    .Seg_D(bcd2_7seg_2_seg_d), .Seg_E(bcd2_7seg_2_seg_e), .Seg_F(bcd2_7seg_2_seg_f), .Seg_G(bcd2_7seg_2_seg_g));
  BCD2_7Seg bcd2_7seg_3 (
    .A0(bin2_bcd_2_d_0), .A1(bin2_bcd_2_d_1), .A2(bin2_bcd_2_d_2), .A3(bin2_bcd_2_d_3),
    .Seg_A(bcd2_7seg_3_seg_a), .Seg_B(bcd2_7seg_3_seg_b), .Seg_C(bcd2_7seg_3_seg_c),
    .Seg_D(bcd2_7seg_3_seg_d), .Seg_E(bcd2_7seg_3_seg_e), .Seg_F(bcd2_7seg_3_seg_f), .Seg_G(bcd2_7seg_3_seg_g));
  BCD2_7Seg bcd2_7seg_4 (
    .A0(bin2_bcd_2_u_0), .A1(bin2_bcd_2_u_1), .A2(bin2_bcd_2_u_2), .A3(bin2_bcd_2_u_3),
    .Seg_A(bcd2_7seg_4_seg_a), .Seg_B(bcd2_7seg_4_seg_b), .Seg_C(bcd2_7seg_4_seg_c),
    .Seg_D(bcd2_7seg_4_seg_d), .Seg_E(bcd2_7seg_4_seg_e), .Seg_F(bcd2_7seg_4_seg_f), .Seg_G(bcd2_7seg_4_seg_g));
  Blinken_Wecker blinken_wecker_1 (
    .Takt(Takt_Wecker_Stellen), .Wecker_Stellen(tastenfehler_1_wecker_stellen), .in_3(bcd2_7seg_1_seg_a),
    .in_4(bcd2_7seg_1_seg_b), .in_5(bcd2_7seg_1_seg_c), .in_6(bcd2_7seg_1_seg_d), .in_7(bcd2_7seg_1_seg_e),
    .in_8(bcd2_7seg_1_seg_f), .in_9(bcd2_7seg_1_seg_g), .in_10(bcd2_7seg_2_seg_a), .in_11(bcd2_7seg_2_seg_b),
    .in_12(bcd2_7seg_2_seg_c), .in_13(bcd2_7seg_2_seg_d), .in_14(bcd2_7seg_2_seg_e),
    .in_15(bcd2_7seg_2_seg_f), .in_16(bcd2_7seg_2_seg_g), .Seg1_A(Seg_1A), .Seg1_B(Seg_1B), .Seg1_C(Seg_1C),
    .Seg1_D(Seg_1D), .Seg1_E(Seg_1E), .Seg1_F(Seg_1F), .Seg1_G(Seg_1G), .Seg2_A(Seg_2A), .Seg2_B(Seg_2B),
    .Seg2_C(Seg_2C), .Seg2_D(Seg_2D), .Seg2_E(Seg_2E), .Seg2_F(Seg_2F), .Seg2_G(Seg_2G));
  Blinken_Wecker blinken_wecker_2 (
    .Takt(Takt_Wecker_Stellen), .Wecker_Stellen(tastenfehler_1_wecker_stellen), .in_3(bcd2_7seg_3_seg_a),
    .in_4(bcd2_7seg_3_seg_b), .in_5(bcd2_7seg_3_seg_c), .in_6(bcd2_7seg_3_seg_d), .in_7(bcd2_7seg_3_seg_e),
    .in_8(bcd2_7seg_3_seg_f), .in_9(bcd2_7seg_3_seg_g), .in_10(bcd2_7seg_4_seg_a), .in_11(bcd2_7seg_4_seg_b),
    .in_12(bcd2_7seg_4_seg_c), .in_13(bcd2_7seg_4_seg_d), .in_14(bcd2_7seg_4_seg_e),
    .in_15(bcd2_7seg_4_seg_f), .in_16(bcd2_7seg_4_seg_g), .Seg1_A(Seg_3A), .Seg1_B(Seg_3B), .Seg1_C(Seg_3C),
    .Seg1_D(Seg_3D), .Seg1_E(Seg_3E), .Seg1_F(Seg_3F), .Seg1_G(Seg_3G), .Seg2_A(Seg_4A), .Seg2_B(Seg_4B),
    .Seg2_C(Seg_4C), .Seg2_D(Seg_4D), .Seg2_E(Seg_4E), .Seg2_F(Seg_4F), .Seg2_G(Seg_4G));
endmodule

module Multiplex_Std_Tag (
  input  Eingangstaste_Min_Sek,
  input  Eingangstaste_Tag_Monat,
  input  Eingangstaste_Jahr,
  input  Wecker_Stellen,
  input  Tag_Bit0,
  input  Tag_Bit1,
  input  Tag_Bit2,
  input  Tag_Bit3,
  input  Tag_Bit4,
  input  Std_Bit0,
  input  Std_Bit1,
  input  Std_Bit2,
  input  Std_Bit3,
  input  Std_Bit4,
  input  Wecker_Std_Bit_0,
  input  Wecker_Std_Bit_1,
  input  Wecker_Std_Bit_2,
  input  Wecker_Std_Bit_3,
  input  Wecker_Std_Bit_4,
  output Bit0,
  output Bit1,
  output Bit2,
  output Bit3,
  output Bit4
);

  wire and_1_out, and_2_out, and_3_out, and_4_out, and_5_out, and_6_out, and_7_out, and_8_out, and_9_out,
       and_10_out, and_11_out, and_12_out, and_13_out, and_14_out, and_15_out;

  and and_1 (and_1_out, Tag_Bit0, ~Eingangstaste_Jahr, Eingangstaste_Tag_Monat, ~Eingangstaste_Min_Sek);  // AND_Gate
  and and_2 (and_2_out, Std_Bit0, ~Eingangstaste_Jahr, ~Eingangstaste_Tag_Monat, ~Eingangstaste_Min_Sek, ~Wecker_Stellen);  // AND_Gate
  and and_3 (and_3_out, Tag_Bit1, ~Eingangstaste_Jahr, Eingangstaste_Tag_Monat, ~Eingangstaste_Min_Sek);  // AND_Gate
  and and_4 (and_4_out, Std_Bit1, ~Eingangstaste_Jahr, ~Eingangstaste_Tag_Monat, ~Eingangstaste_Min_Sek, ~Wecker_Stellen);  // AND_Gate
  and and_5 (and_5_out, Tag_Bit2, ~Eingangstaste_Jahr, Eingangstaste_Tag_Monat, ~Eingangstaste_Min_Sek);  // AND_Gate
  and and_6 (and_6_out, Std_Bit2, ~Eingangstaste_Jahr, ~Eingangstaste_Tag_Monat, ~Eingangstaste_Min_Sek, ~Wecker_Stellen);  // AND_Gate
  and and_7 (and_7_out, Tag_Bit3, ~Eingangstaste_Jahr, Eingangstaste_Tag_Monat, ~Eingangstaste_Min_Sek);  // AND_Gate
  and and_8 (and_8_out, Std_Bit3, ~Eingangstaste_Jahr, ~Eingangstaste_Tag_Monat, ~Eingangstaste_Min_Sek, ~Wecker_Stellen);  // AND_Gate
  and and_9 (and_9_out, Tag_Bit4, ~Eingangstaste_Jahr, Eingangstaste_Tag_Monat, ~Eingangstaste_Min_Sek);  // AND_Gate
  and and_10 (and_10_out, Std_Bit4, ~Eingangstaste_Jahr, ~Eingangstaste_Tag_Monat, ~Eingangstaste_Min_Sek, ~Wecker_Stellen);  // AND_Gate
  and and_11 (and_11_out, Wecker_Stellen, Wecker_Std_Bit_0);
  and and_12 (and_12_out, Wecker_Stellen, Wecker_Std_Bit_1);
  and and_13 (and_13_out, Wecker_Stellen, Wecker_Std_Bit_2);
  and and_14 (and_14_out, Wecker_Stellen, Wecker_Std_Bit_3);
  and and_15 (and_15_out, Wecker_Stellen, Wecker_Std_Bit_4);
  or or_1 (Bit0, and_1_out, and_11_out, and_2_out);
  or or_2 (Bit1, and_3_out, and_12_out, and_4_out);
  or or_3 (Bit2, and_5_out, and_13_out, and_6_out);
  or or_4 (Bit3, and_7_out, and_14_out, and_8_out);
  or or_5 (Bit4, and_9_out, and_15_out, and_10_out);
endmodule

module Multiplex_Min_Monat (
  input  Eingangstaste_Tag_Monat,
  input  Eingangstaste_Jahr,
  input  Wecker_Stellen,
  input  Monat_Bit0,
  input  Monat_Bit1,
  input  Monat_Bit2,
  input  Monat_Bit3,
  input  Min_Bit0,
  input  Min_Bit1,
  input  Min_Bit2,
  input  Min_Bit3,
  input  Min_Bit4,
  input  Min_Bit5,
  input  Wecker_Min_Bit_0,
  input  Wecker_Min_Bit_1,
  input  Wecker_Min_Bit_2,
  input  Wecker_Min_Bit_3,
  input  Wecker_Min_Bit_4,
  input  Wecker_Min_Bit_5,
  output Bit0,
  output Bit1,
  output Bit2,
  output Bit3,
  output Bit4,
  output Bit5
);

  wire and_1_out, and_2_out, and_3_out, and_4_out, and_5_out, and_6_out, and_7_out, and_8_out, and_9_out,
       and_10_out, and_11_out, and_12_out, and_13_out, and_14_out, and_15_out, and_16_out;

  and and_1 (and_1_out, Monat_Bit0, ~Eingangstaste_Jahr, Eingangstaste_Tag_Monat);  // AND_Gate
  and and_2 (and_2_out, Min_Bit0, ~Eingangstaste_Jahr, ~Wecker_Stellen, ~Eingangstaste_Tag_Monat);  // AND_Gate
  and and_3 (and_3_out, Monat_Bit1, ~Eingangstaste_Jahr, Eingangstaste_Tag_Monat);  // AND_Gate
  and and_4 (and_4_out, Min_Bit1, ~Eingangstaste_Jahr, ~Wecker_Stellen, ~Eingangstaste_Tag_Monat);  // AND_Gate
  and and_5 (and_5_out, Monat_Bit2, ~Eingangstaste_Jahr, Eingangstaste_Tag_Monat);  // AND_Gate
  and and_6 (and_6_out, Min_Bit2, ~Eingangstaste_Jahr, ~Wecker_Stellen, ~Eingangstaste_Tag_Monat);  // AND_Gate
  and and_7 (and_7_out, Monat_Bit3, ~Eingangstaste_Jahr, Eingangstaste_Tag_Monat);  // AND_Gate
  and and_8 (and_8_out, Min_Bit3, ~Eingangstaste_Jahr, ~Wecker_Stellen, ~Eingangstaste_Tag_Monat);  // AND_Gate
  and and_9 (and_9_out, Min_Bit4, ~Eingangstaste_Jahr, ~Wecker_Stellen, ~Eingangstaste_Tag_Monat);  // AND_Gate
  and and_10 (and_10_out, Min_Bit5, ~Eingangstaste_Jahr, ~Wecker_Stellen, ~Eingangstaste_Tag_Monat);  // AND_Gate
  and and_11 (and_11_out, Wecker_Stellen, Wecker_Min_Bit_0);
  and and_12 (and_12_out, Wecker_Stellen, Wecker_Min_Bit_1);
  and and_13 (and_13_out, Wecker_Stellen, Wecker_Min_Bit_2);
  and and_14 (and_14_out, Wecker_Stellen, Wecker_Min_Bit_3);
  and and_15 (and_15_out, Wecker_Stellen, Wecker_Min_Bit_4);
  and and_16 (and_16_out, Wecker_Stellen, Wecker_Min_Bit_5);
  or or_1 (Bit0, and_1_out, and_11_out, and_2_out);
  or or_2 (Bit1, and_3_out, and_12_out, and_4_out);
  or or_3 (Bit2, and_5_out, and_13_out, and_6_out);
  or or_4 (Bit3, and_7_out, and_14_out, and_8_out);
  or or_5 (Bit4, and_9_out, and_15_out);
  or or_6 (Bit5, and_10_out, and_16_out);
endmodule

module Multiplex_Jahr_Sekunden (
  input  Eingangstaste_Jahr,
  input  Eingangstaste_Min_Sek,
  input  Jahr_Bit0,
  input  Jahr_Bit1,
  input  Jahr_Bit2,
  input  Jahr_Bit3,
  input  Jahr_Bit4,
  input  Jahr_Bit5,
  input  Jahr_Bit6,
  input  Sekunden_Bit_0,
  input  Sekunden_Bit_1,
  input  Sekunden_Bit_2,
  input  Sekunden_Bit_3,
  input  Sekunden_Bit_4,
  input  Sekunden_Bit_5,
  output Bit0,
  output Bit1,
  output Bit2,
  output Bit3,
  output Bit4,
  output Bit5,
  output Bit6
);

  wire and_1_out, and_2_out, and_3_out, and_4_out, and_5_out, and_6_out, multiplex_sekunden_1_bit_0,
       multiplex_sekunden_1_bit_1, multiplex_sekunden_1_bit_2, multiplex_sekunden_1_bit_3,
       multiplex_sekunden_1_bit_4, multiplex_sekunden_1_bit_5;

  and and_1 (and_1_out, Jahr_Bit0, Eingangstaste_Jahr);
  and and_2 (and_2_out, Jahr_Bit1, Eingangstaste_Jahr);
  and and_3 (and_3_out, Jahr_Bit2, Eingangstaste_Jahr);
  and and_4 (and_4_out, Jahr_Bit3, Eingangstaste_Jahr);
  and and_5 (and_5_out, Jahr_Bit4, Eingangstaste_Jahr);
  and and_6 (and_6_out, Jahr_Bit5, Eingangstaste_Jahr);
  and and_7 (Bit6, Jahr_Bit6, Eingangstaste_Jahr);
  Multiplex_Sekunden multiplex_sekunden_1 (
    .Taste_Min_Sek(Eingangstaste_Min_Sek), .Sek_Bit_0(Sekunden_Bit_0), .Sek_Bit_1(Sekunden_Bit_1),
    .Sek_Bit_2(Sekunden_Bit_2), .Sek_Bit_3(Sekunden_Bit_3), .Sek_Bit_4(Sekunden_Bit_4),
    .Sek_Bit_5(Sekunden_Bit_5), .Bit_0(multiplex_sekunden_1_bit_0), .Bit_1(multiplex_sekunden_1_bit_1),
    .Bit_2(multiplex_sekunden_1_bit_2), .Bit_3(multiplex_sekunden_1_bit_3),
    .Bit_4(multiplex_sekunden_1_bit_4), .Bit_5(multiplex_sekunden_1_bit_5));
  or or_1 (Bit0, and_1_out, multiplex_sekunden_1_bit_0);
  or or_2 (Bit1, and_2_out, multiplex_sekunden_1_bit_1);
  or or_3 (Bit2, and_3_out, multiplex_sekunden_1_bit_2);
  or or_4 (Bit3, and_4_out, multiplex_sekunden_1_bit_3);
  or or_5 (Bit4, and_5_out, multiplex_sekunden_1_bit_4);
  or or_6 (Bit5, and_6_out, multiplex_sekunden_1_bit_5);
endmodule

module Verknuepfung_min_mon_jahr (
  input  in_1,
  input  in_2,
  input  in_3,
  input  in_4,
  input  in_5,
  input  in_6,
  input  in_7,
  input  in_8,
  input  in_9,
  input  in_10,
  input  in_11,
  input  in_12,
  output out_13,
  output out_14,
  output out_15,
  output out_16,
  output out_17,
  output out_18
);

  or or_1 (out_13, in_1, in_2);
  or or_2 (out_14, in_3, in_4);
  or or_3 (out_15, in_5, in_6);
  or or_4 (out_16, in_7, in_8);
  or or_5 (out_17, in_9, in_10);
  or or_6 (out_18, in_11, in_12);
endmodule

module Testing7Seg (
  input  in_1,
  input  in_2,
  input  in_3,
  input  in_4,
  input  in_5,
  input  in_6,
  input  [4:0] in_7,
  input  [4:0] in_8,
  input  [5:0] in_9,
  input  [5:0] in_10,
  input  [5:0] in_11,
  input  [4:0] in_12,
  input  [3:0] in_13,
  input  [6:0] in_14
);

  wire hauptschaltung_7seg_anzeige_1_p15, hauptschaltung_7seg_anzeige_1_p16,
       hauptschaltung_7seg_anzeige_1_p17, hauptschaltung_7seg_anzeige_1_p18,
       hauptschaltung_7seg_anzeige_1_p19, hauptschaltung_7seg_anzeige_1_p20,
       hauptschaltung_7seg_anzeige_1_p21, hauptschaltung_7seg_anzeige_1_p22,
       hauptschaltung_7seg_anzeige_1_p23, hauptschaltung_7seg_anzeige_1_p24,
       hauptschaltung_7seg_anzeige_1_p25, hauptschaltung_7seg_anzeige_1_p26,
       hauptschaltung_7seg_anzeige_1_p27, hauptschaltung_7seg_anzeige_1_p28,
       hauptschaltung_7seg_anzeige_1_p29, hauptschaltung_7seg_anzeige_1_p30,
       hauptschaltung_7seg_anzeige_1_p31, hauptschaltung_7seg_anzeige_1_p32,
       hauptschaltung_7seg_anzeige_1_p33, hauptschaltung_7seg_anzeige_1_p34,
       hauptschaltung_7seg_anzeige_1_p35, hauptschaltung_7seg_anzeige_1_p36,
       hauptschaltung_7seg_anzeige_1_p37, hauptschaltung_7seg_anzeige_1_p38;

  _7_Segment_Display u_7_segment_display_1 (
    .f(hauptschaltung_7seg_anzeige_1_p15), .a(hauptschaltung_7seg_anzeige_1_p17),
    .b(hauptschaltung_7seg_anzeige_1_p19), .d(hauptschaltung_7seg_anzeige_1_p16),
    .c(hauptschaltung_7seg_anzeige_1_p18), .dp(hauptschaltung_7seg_anzeige_1_p20));  // open: g, e
  _7_Segment_Display u_7_segment_display_2 (
    .f(hauptschaltung_7seg_anzeige_1_p21), .a(hauptschaltung_7seg_anzeige_1_p23),
    .b(hauptschaltung_7seg_anzeige_1_p25), .d(hauptschaltung_7seg_anzeige_1_p22),
    .c(hauptschaltung_7seg_anzeige_1_p24), .dp(hauptschaltung_7seg_anzeige_1_p26));  // open: g, e
  _7_Segment_Display u_7_segment_display_3 (
    .f(hauptschaltung_7seg_anzeige_1_p27), .a(hauptschaltung_7seg_anzeige_1_p29),
    .b(hauptschaltung_7seg_anzeige_1_p31), .d(hauptschaltung_7seg_anzeige_1_p28),
    .c(hauptschaltung_7seg_anzeige_1_p30), .dp(hauptschaltung_7seg_anzeige_1_p32));  // open: g, e
  _7_Segment_Display u_7_segment_display_4 (
    .f(hauptschaltung_7seg_anzeige_1_p33), .a(hauptschaltung_7seg_anzeige_1_p35),
    .b(hauptschaltung_7seg_anzeige_1_p37), .d(hauptschaltung_7seg_anzeige_1_p34),
    .c(hauptschaltung_7seg_anzeige_1_p36), .dp(hauptschaltung_7seg_anzeige_1_p38));  // open: g, e
  // Hauptschaltung_7Seg_Anzeige hauptschaltung_7seg_anzeige_1: pin names not known; wires that end beside it: in_1, in_2, in_3, in_4, in_5, in_6, in_7, in_8, in_9, in_10, in_11, in_12, in_13, in_14, hauptschaltung_7seg_anzeige_1_p15, hauptschaltung_7seg_anzeige_1_p16, hauptschaltung_7seg_anzeige_1_p17, hauptschaltung_7seg_anzeige_1_p18, hauptschaltung_7seg_anzeige_1_p19, hauptschaltung_7seg_anzeige_1_p20, hauptschaltung_7seg_anzeige_1_p21, hauptschaltung_7seg_anzeige_1_p22, hauptschaltung_7seg_anzeige_1_p23, hauptschaltung_7seg_anzeige_1_p24, hauptschaltung_7seg_anzeige_1_p25, hauptschaltung_7seg_anzeige_1_p26, hauptschaltung_7seg_anzeige_1_p27, hauptschaltung_7seg_anzeige_1_p28, hauptschaltung_7seg_anzeige_1_p29, hauptschaltung_7seg_anzeige_1_p30, hauptschaltung_7seg_anzeige_1_p31, hauptschaltung_7seg_anzeige_1_p32, hauptschaltung_7seg_anzeige_1_p33, hauptschaltung_7seg_anzeige_1_p34, hauptschaltung_7seg_anzeige_1_p35, hauptschaltung_7seg_anzeige_1_p36, hauptschaltung_7seg_anzeige_1_p37, hauptschaltung_7seg_anzeige_1_p38
endmodule

module BCD2_7Seg (
  input  A0,
  input  A1,
  input  A2,
  input  A3,
  output Seg_A,
  output Seg_B,
  output Seg_C,
  output Seg_D,
  output Seg_E,
  output Seg_F,
  output Seg_G
);

  wire nand_1_out, nand_2_out, nand_3_out, nand_4_out, nor_1_out, nor_2_out, nor_3_out, nor_4_out, nor_5_out,
       nor_6_out, nor_7_out, nor_8_out, nor_9_out, nor_10_out, nor_11_out, nor_12_out, nor_13_out,
       nor_14_out, nor_15_out, nor_16_out, nor_17_out, nor_18_out, nor_19_out, nor_20_out, nor_21_out,
       nor_22_out, nor_23_out, nor_24_out, nor_25_out, nor_26_out, nor_27_out, nor_28_out, nor_29_out,
       nor_33_out;

  nor nor_1 (nor_1_out, A0, A0);
  nor nor_2 (nor_2_out, A2, A2);
  nor nor_3 (nor_3_out, A0, A0);
  nor nor_4 (nor_4_out, A2, A2);
  nor nor_5 (nor_5_out, A1, A1);
  nor nor_6 (nor_6_out, A2, A2);
  nor nor_7 (nor_7_out, A1, A1);
  nor nor_8 (nor_8_out, A0, A0);
  nor nor_9 (nor_9_out, A2, A2);
  nor nor_10 (nor_10_out, A0, A0);
  nor nor_11 (nor_11_out, A1, A1);
  nor nor_12 (nor_12_out, A2, A2);
  nand nand_1 (nand_1_out, A0, A0);
  nand nand_2 (nand_2_out, A2, A2);
  nor nor_13 (nor_13_out, A1, A1);
  nor nor_14 (nor_14_out, A0, A0);
  nor nor_15 (nor_15_out, A1, A2, A3);
  nor nor_16 (nor_16_out, A0, A0);
  nor nor_17 (nor_17_out, A1, A1);
  nor nor_18 (nor_18_out, A2, A2);
  nor nor_19 (nor_19_out, nor_1_out, A1, A2, A3);
  nor nor_20 (nor_20_out, A3, A0, A1, nor_2_out);
  nor nor_21 (nor_21_out, nor_3_out, A1, A3, nor_4_out);
  nor nor_22 (nor_22_out, nor_5_out, nor_6_out, A0, A3);
  nor nor_23 (nor_23_out, nor_7_out, A0, A2, A3);
  nor nor_24 (nor_24_out, nor_8_out, A1, A2, A3);
  nor nor_25 (nor_25_out, nor_9_out, A0, A1, A3);
  nand nand_3 (nand_3_out, A1, nand_1_out);
  nand nand_4 (nand_4_out, nand_1_out, nand_2_out);
  nor nor_26 (nor_26_out, A2, nor_13_out);
  nor nor_27 (nor_27_out, nor_13_out, nor_14_out);
  nor nor_28 (nor_28_out, nor_14_out, A2, A3);
  nor nor_29 (nor_29_out, nor_16_out, nor_17_out, nor_18_out);
  nor nor_30 (Seg_A, nor_19_out, nor_20_out);
  nor nor_31 (Seg_B, nor_21_out, nor_22_out);
  nor nor_32 (Seg_C, nor_23_out, nor_23_out);
  nor nor_33 (nor_33_out, nor_10_out, nor_11_out, nor_12_out, A3);
  nand nand_5 (Seg_E, nand_3_out, nand_4_out);
  nor nor_34 (Seg_F, nor_26_out, nor_27_out, nor_28_out);
  nor nor_35 (Seg_G, nor_15_out, nor_29_out);
  nor nor_36 (Seg_D, nor_24_out, nor_25_out, nor_33_out);
endmodule

module Bin2_BCD (
  input  A_0,
  input  A_1,
  input  A_2,
  input  A_3,
  input  A_4,
  input  A_5,
  input  A_6,
  input  A_7,
  input  A_8,
  output C_0,
  output C_1,
  output C_2,
  output D_0,
  output D_1,
  output D_2,
  output D_3,
  output U_0,
  output U_1,
  output U_2,
  output U_3
);

  wire bcd_teil_1_s_0, bcd_teil_1_s_1, bcd_teil_1_s_2, bcd_teil_3_s_0, bcd_teil_3_s_1, bcd_teil_3_s_2,
       bcd_teil_3_s_3, bcd_teil_4_s_0, bcd_teil_4_s_1, bcd_teil_4_s_2, bcd_teil_4_s_3, bcd_teil_5_s_0,
       bcd_teil_5_s_1, bcd_teil_5_s_2, bcd_teil_5_s_3, bcd_teil_6_s_0, bcd_teil_6_s_1, bcd_teil_6_s_2,
       bcd_teil_6_s_3, bcd_teil_7_s_0, bcd_teil_7_s_1, bcd_teil_7_s_2, bcd_teil_7_s_3, bcd_teil_9_s_0,
       bcd_teil_9_s_1, bcd_teil_9_s_2, bcd_teil_9_s_3, bcd_teil_10_s_0, bcd_teil_10_s_1, bcd_teil_10_s_2,
       bcd_teil_10_s_3;

  BCD_Teil bcd_teil_1 (
    .A_0(bcd_teil_6_s_3), .S_0(bcd_teil_1_s_0), .S_1(bcd_teil_1_s_1), .S_2(bcd_teil_1_s_2));  // open: A_1, A_2, A_3, S_3
  BCD_Teil bcd_teil_2 (
    .A_0(bcd_teil_7_s_3), .A_1(bcd_teil_1_s_0), .A_2(bcd_teil_1_s_1), .A_3(bcd_teil_1_s_2), .S_0(C_1),
    .S_1(C_2));  // open: S_2, S_3
  BCD_Teil bcd_teil_3 (
    .A_0(A_6), .A_1(A_7), .A_2(A_8), .S_0(bcd_teil_3_s_0), .S_1(bcd_teil_3_s_1), .S_2(bcd_teil_3_s_2),
    .S_3(bcd_teil_3_s_3));  // open: A_3
  BCD_Teil bcd_teil_4 (
    .A_0(A_5), .A_1(bcd_teil_3_s_0), .A_2(bcd_teil_3_s_1), .A_3(bcd_teil_3_s_2), .S_0(bcd_teil_4_s_0),
    .S_1(bcd_teil_4_s_1), .S_2(bcd_teil_4_s_2), .S_3(bcd_teil_4_s_3));
  BCD_Teil bcd_teil_5 (
    .A_0(A_4), .A_1(bcd_teil_4_s_0), .A_2(bcd_teil_4_s_1), .A_3(bcd_teil_4_s_2), .S_0(bcd_teil_5_s_0),
    .S_1(bcd_teil_5_s_1), .S_2(bcd_teil_5_s_2), .S_3(bcd_teil_5_s_3));
  BCD_Teil bcd_teil_6 (
    .A_0(bcd_teil_5_s_3), .A_1(bcd_teil_4_s_3), .A_2(bcd_teil_3_s_3), .S_0(bcd_teil_6_s_0),
    .S_1(bcd_teil_6_s_1), .S_2(bcd_teil_6_s_2), .S_3(bcd_teil_6_s_3));  // open: A_3
  BCD_Teil bcd_teil_7 (
    .A_0(bcd_teil_9_s_3), .A_1(bcd_teil_6_s_0), .A_2(bcd_teil_6_s_1), .A_3(bcd_teil_6_s_2),
    .S_0(bcd_teil_7_s_0), .S_1(bcd_teil_7_s_1), .S_2(bcd_teil_7_s_2), .S_3(bcd_teil_7_s_3));
  BCD_Teil bcd_teil_8 (
    .A_0(bcd_teil_10_s_3), .A_1(bcd_teil_7_s_0), .A_2(bcd_teil_7_s_1), .A_3(bcd_teil_7_s_2), .S_0(D_1),
    .S_1(D_2), .S_2(D_3), .S_3(C_0));
  BCD_Teil bcd_teil_9 (
    .A_0(A_3), .A_1(bcd_teil_5_s_0), .A_2(bcd_teil_5_s_1), .A_3(bcd_teil_5_s_2), .S_0(bcd_teil_9_s_0),
    .S_1(bcd_teil_9_s_1), .S_2(bcd_teil_9_s_2), .S_3(bcd_teil_9_s_3));
  BCD_Teil bcd_teil_10 (
    .A_0(A_2), .A_1(bcd_teil_9_s_0), .A_2(bcd_teil_9_s_1), .A_3(bcd_teil_9_s_2), .S_0(bcd_teil_10_s_0),
    .S_1(bcd_teil_10_s_1), .S_2(bcd_teil_10_s_2), .S_3(bcd_teil_10_s_3));
  BCD_Teil bcd_teil_11 (
    .A_0(A_1), .A_1(bcd_teil_10_s_0), .A_2(bcd_teil_10_s_1), .A_3(bcd_teil_10_s_2), .S_0(U_1), .S_1(U_2),
    .S_2(U_3), .S_3(D_0));

  assign U_0 = A_0;
endmodule

module BCD_Teil (
  input  A_0,
  input  A_1,
  input  A_2,
  input  A_3,
  output S_0,
  output S_1,
  output S_2,
  output S_3
);

  wire and_1_out, and_2_out, and_3_out, and_4_out, and_5_out, and_6_out, and_7_out, not_1_out, not_2_out,
       not_3_out, not_4_out, or_1_out, or_2_out, or_3_out;

  not not_1 (not_1_out, A_0);
  not not_2 (not_2_out, A_1);
  not not_3 (not_3_out, A_2);
  not not_4 (not_4_out, A_3);
  and and_1 (and_1_out, A_0, not_3_out, not_4_out);
  and and_2 (and_2_out, not_1_out, A_3);
  and and_3 (and_3_out, not_1_out, A_1, A_2);
  or or_1 (or_1_out, A_1, A_3);
  or or_2 (or_2_out, A_0, not_3_out);
  or or_3 (or_3_out, not_1_out, not_4_out);
  and and_4 (and_4_out, not_1_out, not_2_out, A_2);
  and and_5 (and_5_out, A_0, A_3);
  and and_6 (and_6_out, A_0, A_2);
  and and_7 (and_7_out, A_1, A_2);
  or or_4 (S_0, and_1_out, and_2_out, and_3_out);
  and and_8 (S_1, or_1_out, or_2_out, or_3_out);
  or or_5 (S_2, and_4_out, and_5_out);
  or or_6 (S_3, and_6_out, and_7_out, A_3);
endmodule

module Umschaltung_Min (
  input  Taste_Min_Sek,
  input  Bit_0,
  input  Bit_1,
  input  Bit_2,
  input  Bit_3,
  input  Bit_4,
  input  Bit_5,
  output Seg1_Bit_0,
  output Seg1_Bit_1,
  output Seg1_Bit_2,
  output Seg1_Bit_3,
  output Seg1_Bit_4,
  output Seg1_Bit_5,
  output Seg2_Bit_0,
  output Seg2_Bit_1,
  output Seg2_Bit_2,
  output Seg2_Bit_3,
  output Seg2_Bit_4,
  output Seg2_Bit_5
);

  and and_1 (Seg1_Bit_0, Taste_Min_Sek, Bit_0);
  and and_2 (Seg2_Bit_0, ~Taste_Min_Sek, Bit_0);  // AND_Gate
  and and_3 (Seg1_Bit_1, Taste_Min_Sek, Bit_1);
  and and_4 (Seg2_Bit_1, ~Taste_Min_Sek, Bit_1);  // AND_Gate
  and and_5 (Seg1_Bit_2, Taste_Min_Sek, Bit_2);
  and and_6 (Seg2_Bit_2, ~Taste_Min_Sek, Bit_2);  // AND_Gate
  and and_7 (Seg1_Bit_3, Taste_Min_Sek, Bit_3);
  and and_8 (Seg2_Bit_3, ~Taste_Min_Sek, Bit_3);  // AND_Gate
  and and_9 (Seg1_Bit_4, Taste_Min_Sek, Bit_4);
  and and_10 (Seg2_Bit_4, ~Taste_Min_Sek, Bit_4);  // AND_Gate
  and and_11 (Seg1_Bit_5, Taste_Min_Sek, Bit_5);
  and and_12 (Seg2_Bit_5, ~Taste_Min_Sek, Bit_5);  // AND_Gate
endmodule

module Multiplex_Sekunden (
  input  Taste_Min_Sek,
  input  Sek_Bit_0,
  input  Sek_Bit_1,
  input  Sek_Bit_2,
  input  Sek_Bit_3,
  input  Sek_Bit_4,
  input  Sek_Bit_5,
  output Bit_0,
  output Bit_1,
  output Bit_2,
  output Bit_3,
  output Bit_4,
  output Bit_5
);

  and and_1 (Bit_0, Sek_Bit_0, Taste_Min_Sek);
  and and_2 (Bit_1, Sek_Bit_1, Taste_Min_Sek);
  and and_3 (Bit_2, Sek_Bit_2, Taste_Min_Sek);
  and and_4 (Bit_3, Sek_Bit_3, Taste_Min_Sek);
  and and_5 (Bit_4, Sek_Bit_4, Taste_Min_Sek);
  and and_6 (Bit_5, Sek_Bit_5, Taste_Min_Sek);
endmodule

module Tastenfehler (
  input  Taste_Gecko_Min_Sek,
  input  Taste_Gecko_Tag_Mon,
  input  Taste_Gecko_Jahr,
  input  Schalter_Gecko_Wecker_Stellen,
  output Taste_Min_Sek,
  output Taste_Tag_Mon,
  output Taste_Jahr,
  output Wecker_Stellen
);

  and and_1 (Taste_Min_Sek, Taste_Gecko_Min_Sek, ~Taste_Gecko_Tag_Mon, ~Taste_Gecko_Jahr, ~Schalter_Gecko_Wecker_Stellen);  // AND_Gate
  and and_2 (Taste_Tag_Mon, ~Taste_Gecko_Min_Sek, Taste_Gecko_Tag_Mon, ~Taste_Gecko_Jahr, ~Schalter_Gecko_Wecker_Stellen);  // AND_Gate
  and and_3 (Taste_Jahr, ~Taste_Gecko_Min_Sek, ~Taste_Gecko_Tag_Mon, Taste_Gecko_Jahr, ~Schalter_Gecko_Wecker_Stellen);  // AND_Gate

  assign Wecker_Stellen = Schalter_Gecko_Wecker_Stellen;
endmodule

module Weckfunktion_Zeitvergleich (
  input  Wecker_Ein_Aus,
  input  Stunde_Aktuell_0,
  input  Stunde_Aktuell_1,
  input  Stunde_Aktuell_2,
  input  Stunde_Aktuell_3,
  input  Stunde_Aktuell_4,
  input  Stunde_Wecker_0,
  input  Stunde_Wecker_1,
  input  Stunde_Wecker_2,
  input  Stunde_Wecker_3,
  input  Stunde_Wecker_4,
  input  MInute_Aktuell_0,
  input  MInute_Aktuell_1,
  input  MInute_Aktuell_2,
  input  MInute_Aktuell_3,
  input  MInute_Aktuell_4,
  input  MInute_Aktuell_5,
  input  MInute_Wecker_0,
  input  MInute_Wecker_1,
  input  MInute_Wecker_2,
  input  MInute_Wecker_3,
  input  MInute_Wecker_4,
  input  MInute_Wecker_5,
  output Nach_LED_Anzeige_Weckfunktion
);

  wire and_1_out, and_3_out, xnor_1_out, xnor_2_out, xnor_3_out, xnor_4_out, xnor_5_out, xnor_6_out,
       xnor_7_out, xnor_8_out, xnor_9_out, xnor_10_out, xnor_11_out;

  xnor xnor_1 (xnor_1_out, Stunde_Aktuell_0, Stunde_Wecker_0);
  xnor xnor_2 (xnor_2_out, Stunde_Aktuell_1, Stunde_Wecker_1);
  xnor xnor_3 (xnor_3_out, Stunde_Aktuell_2, Stunde_Wecker_2);
  xnor xnor_4 (xnor_4_out, Stunde_Aktuell_3, Stunde_Wecker_3);
  xnor xnor_5 (xnor_5_out, Stunde_Aktuell_4, Stunde_Wecker_4);
  xnor xnor_6 (xnor_6_out, MInute_Aktuell_0, MInute_Wecker_0);
  xnor xnor_7 (xnor_7_out, MInute_Aktuell_1, MInute_Wecker_1);
  xnor xnor_8 (xnor_8_out, MInute_Aktuell_2, MInute_Wecker_2);
  xnor xnor_9 (xnor_9_out, MInute_Aktuell_3, MInute_Wecker_3);
  xnor xnor_10 (xnor_10_out, MInute_Aktuell_4, MInute_Wecker_4);
  xnor xnor_11 (xnor_11_out, MInute_Aktuell_5, MInute_Wecker_5);
  and and_1 (and_1_out, Wecker_Ein_Aus, xnor_1_out, xnor_2_out, xnor_3_out, xnor_4_out, xnor_5_out);
  and and_2 (Nach_LED_Anzeige_Weckfunktion, and_1_out, and_3_out);
  and and_3 (and_3_out, xnor_6_out, xnor_7_out, xnor_8_out, xnor_9_out, xnor_10_out, xnor_11_out);
endmodule

module Blinken_Wecker (
  input  Takt,
  input  Wecker_Stellen,
  input  in_3,
  input  in_4,
  input  in_5,
  input  in_6,
  input  in_7,
  input  in_8,
  input  in_9,
  input  in_10,
  input  in_11,
  input  in_12,
  input  in_13,
  input  in_14,
  input  in_15,
  input  in_16,
  output Seg1_A,
  output Seg1_B,
  output Seg1_C,
  output Seg1_D,
  output Seg1_E,
  output Seg1_F,
  output Seg1_G,
  output Seg2_A,
  output Seg2_B,
  output Seg2_C,
  output Seg2_D,
  output Seg2_E,
  output Seg2_F,
  output Seg2_G
);

  wire and_1_out, and_2_out, and_3_out, and_4_out, and_5_out, and_6_out, and_7_out, and_8_out, and_9_out,
       and_10_out, and_11_out, and_12_out, and_13_out, and_14_out, and_15_out, and_16_out, and_17_out,
       and_18_out, and_19_out, and_20_out, and_21_out, and_22_out, and_23_out, and_24_out, and_25_out,
       and_26_out, and_27_out, and_28_out;

  and and_1 (and_1_out, ~Wecker_Stellen, in_3);  // AND_Gate
  and and_2 (and_2_out, ~Wecker_Stellen, in_4);  // AND_Gate
  and and_3 (and_3_out, ~Wecker_Stellen, in_5);  // AND_Gate
  and and_4 (and_4_out, ~Wecker_Stellen, in_6);  // AND_Gate
  and and_5 (and_5_out, ~Wecker_Stellen, in_7);  // AND_Gate
  and and_6 (and_6_out, ~Wecker_Stellen, in_8);  // AND_Gate
  and and_7 (and_7_out, ~Wecker_Stellen, in_9);  // AND_Gate
  and and_8 (and_8_out, ~Wecker_Stellen, in_10);  // AND_Gate
  and and_9 (and_9_out, ~Wecker_Stellen, in_11);  // AND_Gate
  and and_10 (and_10_out, ~Wecker_Stellen, in_12);  // AND_Gate
  and and_11 (and_11_out, ~Wecker_Stellen, in_13);  // AND_Gate
  and and_12 (and_12_out, ~Wecker_Stellen, in_14);  // AND_Gate
  and and_13 (and_13_out, ~Wecker_Stellen, in_15);  // AND_Gate
  and and_14 (and_14_out, ~Wecker_Stellen, in_16);  // AND_Gate
  and and_15 (and_15_out, Wecker_Stellen, Takt, in_3);
  and and_16 (and_16_out, Wecker_Stellen, Takt, in_4);
  and and_17 (and_17_out, Wecker_Stellen, Takt, in_5);
  and and_18 (and_18_out, Wecker_Stellen, Takt, in_6);
  and and_19 (and_19_out, Wecker_Stellen, Takt, in_7);
  and and_20 (and_20_out, Wecker_Stellen, Takt, in_8);
  and and_21 (and_21_out, Wecker_Stellen, Takt, in_9);
  and and_22 (and_22_out, Wecker_Stellen, Takt, in_10);
  and and_23 (and_23_out, Wecker_Stellen, Takt, in_11);
  and and_24 (and_24_out, Wecker_Stellen, Takt, in_12);
  and and_25 (and_25_out, Wecker_Stellen, Takt, in_13);
  and and_26 (and_26_out, Wecker_Stellen, Takt, in_14);
  and and_27 (and_27_out, Wecker_Stellen, Takt, in_15);
  and and_28 (and_28_out, Wecker_Stellen, Takt, in_16);
  or or_1 (Seg1_A, and_1_out, and_15_out);
  or or_2 (Seg1_B, and_2_out, and_16_out);
  or or_3 (Seg1_C, and_3_out, and_17_out);
  or or_4 (Seg1_D, and_4_out, and_18_out);
  or or_5 (Seg1_E, and_5_out, and_19_out);
  or or_6 (Seg1_F, and_6_out, and_20_out);
  or or_7 (Seg1_G, and_7_out, and_21_out);
  or or_8 (Seg2_A, and_8_out, and_22_out);
  or or_9 (Seg2_B, and_9_out, and_23_out);
  or or_10 (Seg2_C, and_10_out, and_24_out);
  or or_11 (Seg2_D, and_11_out, and_25_out);
  or or_12 (Seg2_E, and_12_out, and_26_out);
  or or_13 (Seg2_F, and_13_out, and_27_out);
  or or_14 (Seg2_G, and_14_out, and_28_out);
endmodule
