// Logisim project LED_und_7Seg_Anzeige_Final.circ as structural Verilog: 6 circuits, main circuit Part_Buntr1_Final
module Hauptschaltung_LED_Anzeige (
  input  Input_1,
  input  Weckfunktion,
  input  Eingangstaste_Min_Sek,
  input  Eingangstaste_Tag_Monat,
  input  Eingangstaste_Jahr,
  output LED_Rahmen_Rest_Wecker,
  output LED_3_2,
  output LED_3_3,
  output LED_3_7,
  output LED_3_11,
  output LED_4_2,
  output LED_4_4,
  output LED_4_7,
  output LED_4_8,
  output LED_4_9,
  output LED_4_10,
  output LED_4_11,
  output LED_5_2,
  output LED_5_3,
  output LED_5_4,
  output LED_5_5,
  output LED_5_6,
  output LED_5_7,
  output LED_5_8,
  output LED_5_9,
  output LED_5_10,
  output LED_5_11,
  output LED_6_2,
  output LED_6_3,
  output LED_6_4,
  output LED_6_5,
  output LED_6_6,
  output LED_6_7,
  output LED_6_8,
  output LED_6_9,
  output LED_6_10,
  output LED_6_11,
  output LED_7_2,
  output LED_7_4,
  output LED_7_5,
  output LED_7_6,
  output LED_7_7,
  output LED_7_9,
  output LED_7_10,
  output LED_7_11,
  output LED_8_2,
  output LED_8_3,
  output LED_8_5,
  output LED_8_6,
  output LED_8_7,
  output LED_8_8,
  output LED_8_9,
  output LED_8_10,
  output LED_8_11
);

  wire D_und_M_1_led_3_2, D_und_M_1_led_3_3, D_und_M_1_led_3_7, D_und_M_1_led_3_11, D_und_M_1_led_4_2,
       D_und_M_1_led_4_4, D_und_M_1_led_4_7, D_und_M_1_led_4_8, D_und_M_1_led_4_10, D_und_M_1_led_4_11,
       D_und_M_1_led_5_2, D_und_M_1_led_5_5, D_und_M_1_led_5_7, D_und_M_1_led_5_9, D_und_M_1_led_5_11,
       D_und_M_1_led_6_2, D_und_M_1_led_6_5, D_und_M_1_led_6_7, D_und_M_1_led_6_11, D_und_M_1_led_7_2,
       D_und_M_1_led_7_4, D_und_M_1_led_7_7, D_und_M_1_led_7_11, D_und_M_1_led_8_2, D_und_M_1_led_8_3,
       D_und_M_1_led_8_7, D_und_M_1_led_8_11, h_und_m_1_led_3_2, h_und_m_1_led_4_2, h_und_m_1_led_5_2,
       h_und_m_1_led_5_7, h_und_m_1_led_5_8, h_und_m_1_led_5_9, h_und_m_1_led_5_10, h_und_m_1_led_5_11,
       h_und_m_1_led_6_2, h_und_m_1_led_6_3, h_und_m_1_led_6_4, h_und_m_1_led_6_5, h_und_m_1_led_6_7,
       h_und_m_1_led_6_9, h_und_m_1_led_6_11, h_und_m_1_led_7_2, h_und_m_1_led_7_5, h_und_m_1_led_7_7,
       h_und_m_1_led_7_9, h_und_m_1_led_7_11, h_und_m_1_led_8_2, h_und_m_1_led_8_5, h_und_m_1_led_8_7,
       h_und_m_1_led_8_11, m_und_s_1_led_4_8, m_und_s_1_led_4_9, m_und_s_1_led_4_10, m_und_s_1_led_5_2,
       m_und_s_1_led_5_3, m_und_s_1_led_5_4, m_und_s_1_led_5_5, m_und_s_1_led_5_6, m_und_s_1_led_5_8,
       m_und_s_1_led_6_2, m_und_s_1_led_6_4, m_und_s_1_led_6_6, m_und_s_1_led_6_8, m_und_s_1_led_6_9,
       m_und_s_1_led_6_10, m_und_s_1_led_7_2, m_und_s_1_led_7_4, m_und_s_1_led_7_6, m_und_s_1_led_7_10,
       m_und_s_1_led_8_2, m_und_s_1_led_8_6, m_und_s_1_led_8_8, m_und_s_1_led_8_9, m_und_s_1_led_8_10,
       or_1_out, or_2_out, or_3_out, or_4_out, or_5_out, or_6_out, or_7_out, or_8_out, or_9_out, or_10_out,
       or_11_out, or_12_out, or_13_out, or_14_out, or_15_out, or_16_out, or_17_out, or_18_out, or_19_out,
       or_20_out, or_21_out, or_22_out, or_23_out, or_24_out, or_25_out, or_26_out, or_27_out, or_28_out,
       or_29_out, or_30_out, Y_1_led_3_7, Y_1_led_3_11, Y_1_led_4_7, Y_1_led_4_11, Y_1_led_5_8, Y_1_led_5_10,
       Y_1_led_6_9, Y_1_led_7_9, Y_1_led_8_9;

  and and_1 (LED_Rahmen_Rest_Wecker, Input_1, Weckfunktion);
  h_und_m h_und_m_1 (
    .Taste_min_sek(Eingangstaste_Min_Sek), .Taste_tag_mon(Eingangstaste_Tag_Monat),
    .Taste_jahr(Eingangstaste_Jahr), .LED_3_2(h_und_m_1_led_3_2), .LED_4_2(h_und_m_1_led_4_2),
    .LED_5_2(h_und_m_1_led_5_2), .LED_5_7(h_und_m_1_led_5_7), .LED_5_8(h_und_m_1_led_5_8),
    .LED_5_9(h_und_m_1_led_5_9), .LED_5_10(h_und_m_1_led_5_10), .LED_5_11(h_und_m_1_led_5_11),
    .LED_6_2(h_und_m_1_led_6_2), .LED_6_3(h_und_m_1_led_6_3), .LED_6_4(h_und_m_1_led_6_4),
    .LED_6_5(h_und_m_1_led_6_5), .LED_6_7(h_und_m_1_led_6_7), .LED_6_9(h_und_m_1_led_6_9),
    .LED_6_11(h_und_m_1_led_6_11), .LED_7_2(h_und_m_1_led_7_2), .LED_7_5(h_und_m_1_led_7_5),
    .LED_7_7(h_und_m_1_led_7_7), .LED_7_9(h_und_m_1_led_7_9), .LED_7_11(h_und_m_1_led_7_11),
    .LED_8_2(h_und_m_1_led_8_2), .LED_8_5(h_und_m_1_led_8_5), .LED_8_7(h_und_m_1_led_8_7),
    .LED_8_11(h_und_m_1_led_8_11));
  m_und_s m_und_s_1 (
    .Taste_min_sek(Eingangstaste_Min_Sek), .LED_4_8(m_und_s_1_led_4_8), .LED_4_9(m_und_s_1_led_4_9),
    .LED_4_10(m_und_s_1_led_4_10), .LED_5_2(m_und_s_1_led_5_2), .LED_5_3(m_und_s_1_led_5_3),
    .LED_5_4(m_und_s_1_led_5_4), .LED_5_5(m_und_s_1_led_5_5), .LED_5_6(m_und_s_1_led_5_6),
    .LED_5_8(m_und_s_1_led_5_8), .LED_6_2(m_und_s_1_led_6_2), .LED_6_4(m_und_s_1_led_6_4),
    .LED_6_6(m_und_s_1_led_6_6), .LED_6_8(m_und_s_1_led_6_8), .LED_6_9(m_und_s_1_led_6_9),
    .LED_6_10(m_und_s_1_led_6_10), .LED_7_2(m_und_s_1_led_7_2), .LED_7_4(m_und_s_1_led_7_4),
    .LED_7_6(m_und_s_1_led_7_6), .LED_7_10(m_und_s_1_led_7_10), .LED_8_2(m_und_s_1_led_8_2),
    .LED_8_6(m_und_s_1_led_8_6), .LED_8_8(m_und_s_1_led_8_8), .LED_8_9(m_und_s_1_led_8_9),
    .LED_8_10(m_und_s_1_led_8_10));
  D_und_M D_und_M_1 (
    .Taste_Tag_Monat(Eingangstaste_Tag_Monat), .LED_3_2(D_und_M_1_led_3_2), .LED_3_3(D_und_M_1_led_3_3),
    .LED_3_7(D_und_M_1_led_3_7), .LED_3_11(D_und_M_1_led_3_11), .LED_4_2(D_und_M_1_led_4_2),
    .LED_4_4(D_und_M_1_led_4_4), .LED_4_7(D_und_M_1_led_4_7), .LED_4_8(D_und_M_1_led_4_8),
    .LED_4_10(D_und_M_1_led_4_10), .LED_4_11(D_und_M_1_led_4_11), .LED_5_2(D_und_M_1_led_5_2),
    .LED_5_5(D_und_M_1_led_5_5), .LED_5_7(D_und_M_1_led_5_7), .LED_5_9(D_und_M_1_led_5_9),
    .LED_5_11(D_und_M_1_led_5_11), .LED_6_2(D_und_M_1_led_6_2), .LED_6_5(D_und_M_1_led_6_5),
    .LED_6_7(D_und_M_1_led_6_7), .LED_6_11(D_und_M_1_led_6_11), .LED_7_2(D_und_M_1_led_7_2),
    .LED_7_4(D_und_M_1_led_7_4), .LED_7_7(D_und_M_1_led_7_7), .LED_7_11(D_und_M_1_led_7_11),
    .LED_8_2(D_und_M_1_led_8_2), .LED_8_3(D_und_M_1_led_8_3), .LED_8_7(D_und_M_1_led_8_7),
    .LED_8_11(D_und_M_1_led_8_11));
  Y Y_1 (
    .Taste_Jahr(Eingangstaste_Jahr), .LED_3_7(Y_1_led_3_7), .LED_3_11(Y_1_led_3_11), .LED_4_7(Y_1_led_4_7),
    .LED_4_11(Y_1_led_4_11), .LED_5_8(Y_1_led_5_8), .LED_5_10(Y_1_led_5_10), .LED_6_9(Y_1_led_6_9),
    .LED_7_9(Y_1_led_7_9), .LED_8_9(Y_1_led_8_9));
  or or_1 (or_1_out, h_und_m_1_led_3_2, D_und_M_1_led_3_2);
  or or_2 (or_2_out, D_und_M_1_led_3_7, Y_1_led_3_7);
  or or_3 (or_3_out, D_und_M_1_led_3_11, Y_1_led_3_11);
  or or_4 (or_4_out, h_und_m_1_led_4_2, D_und_M_1_led_4_2);
  or or_5 (or_5_out, D_und_M_1_led_4_7, Y_1_led_4_7);
  or or_6 (or_6_out, m_und_s_1_led_4_8, D_und_M_1_led_4_8);
  or or_7 (or_7_out, m_und_s_1_led_4_10, D_und_M_1_led_4_10);
  or or_8 (or_8_out, D_und_M_1_led_4_11, Y_1_led_4_11);
  or or_9 (or_9_out, h_und_m_1_led_5_2, D_und_M_1_led_5_2, m_und_s_1_led_5_2);
  or or_10 (or_10_out, m_und_s_1_led_5_5, D_und_M_1_led_5_5);
  or or_11 (or_11_out, h_und_m_1_led_5_7, D_und_M_1_led_5_7);
  or or_12 (or_12_out, h_und_m_1_led_5_8, m_und_s_1_led_5_8, Y_1_led_5_8);
  or or_13 (or_13_out, h_und_m_1_led_5_9, D_und_M_1_led_5_9);
  or or_14 (or_14_out, h_und_m_1_led_5_10, Y_1_led_5_10);
  or or_15 (or_15_out, h_und_m_1_led_5_11, D_und_M_1_led_5_11);
  or or_16 (or_16_out, h_und_m_1_led_6_2, m_und_s_1_led_6_2, D_und_M_1_led_6_2);
  or or_17 (or_17_out, h_und_m_1_led_6_4, m_und_s_1_led_6_4);
  or or_18 (or_18_out, h_und_m_1_led_6_5, D_und_M_1_led_6_5);
  or or_19 (or_19_out, h_und_m_1_led_6_7, D_und_M_1_led_6_7);
  or or_20 (or_20_out, h_und_m_1_led_6_9, Y_1_led_6_9, m_und_s_1_led_6_9);
  or or_21 (or_21_out, h_und_m_1_led_6_11, D_und_M_1_led_6_11);
  or or_22 (or_22_out, h_und_m_1_led_7_2, m_und_s_1_led_7_2, D_und_M_1_led_7_2);
  or or_23 (or_23_out, m_und_s_1_led_7_4, D_und_M_1_led_7_4);
  or or_24 (or_24_out, D_und_M_1_led_7_7, h_und_m_1_led_7_7);
  or or_25 (or_25_out, h_und_m_1_led_7_9, Y_1_led_7_9);
  or or_26 (or_26_out, h_und_m_1_led_7_11, D_und_M_1_led_7_11);
  or or_27 (or_27_out, h_und_m_1_led_8_2, m_und_s_1_led_8_2, D_und_M_1_led_8_2);
  or or_28 (or_28_out, h_und_m_1_led_8_7, D_und_M_1_led_8_7);
  or or_29 (or_29_out, m_und_s_1_led_8_9, Y_1_led_8_9);
  or or_30 (or_30_out, h_und_m_1_led_8_11, D_und_M_1_led_8_11);
  xor xor_1 (LED_3_2, LED_Rahmen_Rest_Wecker, or_1_out);
  xor xor_2 (LED_3_3, LED_Rahmen_Rest_Wecker, D_und_M_1_led_3_3);
  xor xor_3 (LED_3_7, LED_Rahmen_Rest_Wecker, or_2_out);
  xor xor_4 (LED_3_11, LED_Rahmen_Rest_Wecker, or_3_out);
  xor xor_5 (LED_4_2, LED_Rahmen_Rest_Wecker, or_4_out);
  xor xor_6 (LED_4_4, LED_Rahmen_Rest_Wecker, D_und_M_1_led_4_4);
  xor xor_7 (LED_4_7, LED_Rahmen_Rest_Wecker, or_5_out);
  xor xor_8 (LED_4_8, LED_Rahmen_Rest_Wecker, or_6_out);
  xor xor_9 (LED_4_9, LED_Rahmen_Rest_Wecker, m_und_s_1_led_4_9);
  xor xor_10 (LED_4_10, LED_Rahmen_Rest_Wecker, or_7_out);
  xor xor_11 (LED_4_11, LED_Rahmen_Rest_Wecker, or_8_out);
  xor xor_12 (LED_5_2, LED_Rahmen_Rest_Wecker, or_9_out);
  xor xor_13 (LED_5_3, LED_Rahmen_Rest_Wecker, m_und_s_1_led_5_3);
  xor xor_14 (LED_5_4, LED_Rahmen_Rest_Wecker, m_und_s_1_led_5_4);
  xor xor_15 (LED_5_5, LED_Rahmen_Rest_Wecker, or_10_out);
  xor xor_16 (LED_5_6, LED_Rahmen_Rest_Wecker, m_und_s_1_led_5_6);
  xor xor_17 (LED_5_7, LED_Rahmen_Rest_Wecker, or_11_out);
  xor xor_18 (LED_5_8, LED_Rahmen_Rest_Wecker, or_12_out);
  xor xor_19 (LED_5_9, LED_Rahmen_Rest_Wecker, or_13_out);
  xor xor_20 (LED_5_10, LED_Rahmen_Rest_Wecker, or_14_out);
  xor xor_21 (LED_5_11, LED_Rahmen_Rest_Wecker, or_15_out);
  xor xor_22 (LED_6_2, LED_Rahmen_Rest_Wecker, or_16_out);
  xor xor_23 (LED_6_3, LED_Rahmen_Rest_Wecker, h_und_m_1_led_6_3);
  xor xor_24 (LED_6_4, LED_Rahmen_Rest_Wecker, or_17_out);
  xor xor_25 (LED_6_5, LED_Rahmen_Rest_Wecker, or_18_out);
  xor xor_26 (LED_6_6, LED_Rahmen_Rest_Wecker, m_und_s_1_led_6_6);
  xor xor_27 (LED_6_7, LED_Rahmen_Rest_Wecker, or_19_out);
  xor xor_28 (LED_6_8, LED_Rahmen_Rest_Wecker, m_und_s_1_led_6_8);
  xor xor_29 (LED_6_9, LED_Rahmen_Rest_Wecker, or_20_out);
  xor xor_30 (LED_6_10, LED_Rahmen_Rest_Wecker, m_und_s_1_led_6_10);
  xor xor_31 (LED_6_11, LED_Rahmen_Rest_Wecker, or_21_out);
  xor xor_32 (LED_7_2, LED_Rahmen_Rest_Wecker, or_22_out);
  xor xor_33 (LED_7_4, LED_Rahmen_Rest_Wecker, or_23_out);
  xor xor_34 (LED_7_5, LED_Rahmen_Rest_Wecker, h_und_m_1_led_7_5);
  xor xor_35 (LED_7_6, LED_Rahmen_Rest_Wecker, m_und_s_1_led_7_6);
  xor xor_36 (LED_7_7, LED_Rahmen_Rest_Wecker, or_24_out);
  xor xor_37 (LED_7_9, LED_Rahmen_Rest_Wecker, or_25_out);
  xor xor_38 (LED_7_10, LED_Rahmen_Rest_Wecker, m_und_s_1_led_7_10);
  xor xor_39 (LED_7_11, LED_Rahmen_Rest_Wecker, or_26_out);
  xor xor_40 (LED_8_2, LED_Rahmen_Rest_Wecker, or_27_out);
  xor xor_41 (LED_8_3, LED_Rahmen_Rest_Wecker, D_und_M_1_led_8_3);
  xor xor_42 (LED_8_5, LED_Rahmen_Rest_Wecker, h_und_m_1_led_8_5);
  xor xor_43 (LED_8_6, LED_Rahmen_Rest_Wecker, m_und_s_1_led_8_6);
  xor xor_44 (LED_8_7, LED_Rahmen_Rest_Wecker, or_28_out);
  xor xor_45 (LED_8_8, LED_Rahmen_Rest_Wecker, m_und_s_1_led_8_8);
  xor xor_46 (LED_8_9, LED_Rahmen_Rest_Wecker, or_29_out);
  xor xor_47 (LED_8_10, LED_Rahmen_Rest_Wecker, m_und_s_1_led_8_10);
  xor xor_48 (LED_8_11, LED_Rahmen_Rest_Wecker, or_30_out);
endmodule

module Part_Buntr1_Final (
  input  in_1,
  input  in_2,
  input  in_3,
  input  in_4,
  input  in_5,
  input  in_6,
  input  [4:0] in_7,
  input  [4:0] in_8,
  input  [5:0] in_9,
  input  [5:0] in_10,
  input  [5:0] in_11,
  input  [4:0] in_12,
  input  [3:0] in_13,
  input  [6:0] in_14
);

  wire hauptschaltung_7seg_anzeige_1_jahr_zu_led, hauptschaltung_7seg_anzeige_1_min_sek_zu_led,
       hauptschaltung_7seg_anzeige_1_seg_1a, hauptschaltung_7seg_anzeige_1_seg_1b,
       hauptschaltung_7seg_anzeige_1_seg_1c, hauptschaltung_7seg_anzeige_1_seg_1d,
       hauptschaltung_7seg_anzeige_1_seg_1e, hauptschaltung_7seg_anzeige_1_seg_1f,
       hauptschaltung_7seg_anzeige_1_seg_1g, hauptschaltung_7seg_anzeige_1_seg_2a,
       hauptschaltung_7seg_anzeige_1_seg_2b, hauptschaltung_7seg_anzeige_1_seg_2c,
       hauptschaltung_7seg_anzeige_1_seg_2d, hauptschaltung_7seg_anzeige_1_seg_2e,
       hauptschaltung_7seg_anzeige_1_seg_2f, hauptschaltung_7seg_anzeige_1_seg_2g,
       hauptschaltung_7seg_anzeige_1_seg_3a, hauptschaltung_7seg_anzeige_1_seg_3b,
       hauptschaltung_7seg_anzeige_1_seg_3c, hauptschaltung_7seg_anzeige_1_seg_3d,
       hauptschaltung_7seg_anzeige_1_seg_3e, hauptschaltung_7seg_anzeige_1_seg_3f,
       hauptschaltung_7seg_anzeige_1_seg_3g, hauptschaltung_7seg_anzeige_1_seg_4a,
       hauptschaltung_7seg_anzeige_1_seg_4b, hauptschaltung_7seg_anzeige_1_seg_4c,
       hauptschaltung_7seg_anzeige_1_seg_4d, hauptschaltung_7seg_anzeige_1_seg_4e,
       hauptschaltung_7seg_anzeige_1_seg_4f, hauptschaltung_7seg_anzeige_1_seg_4g,
       hauptschaltung_7seg_anzeige_1_tag_mon_zu_led, hauptschaltung_7seg_anzeige_1_weckerfunktion_zu_led,
       Hauptschaltung_LED_Anzeige_1_led_3_2, Hauptschaltung_LED_Anzeige_1_led_3_3,
       Hauptschaltung_LED_Anzeige_1_led_3_7, Hauptschaltung_LED_Anzeige_1_led_3_11,
       Hauptschaltung_LED_Anzeige_1_led_4_2, Hauptschaltung_LED_Anzeige_1_led_4_4,
       Hauptschaltung_LED_Anzeige_1_led_4_7, Hauptschaltung_LED_Anzeige_1_led_4_8,
       Hauptschaltung_LED_Anzeige_1_led_4_9, Hauptschaltung_LED_Anzeige_1_led_4_10,
       Hauptschaltung_LED_Anzeige_1_led_4_11, Hauptschaltung_LED_Anzeige_1_led_5_2,
       Hauptschaltung_LED_Anzeige_1_led_5_3, Hauptschaltung_LED_Anzeige_1_led_5_4,
       Hauptschaltung_LED_Anzeige_1_led_5_5, Hauptschaltung_LED_Anzeige_1_led_5_6,
       Hauptschaltung_LED_Anzeige_1_led_5_7, Hauptschaltung_LED_Anzeige_1_led_5_8,
       Hauptschaltung_LED_Anzeige_1_led_5_9, Hauptschaltung_LED_Anzeige_1_led_5_10,
       Hauptschaltung_LED_Anzeige_1_led_5_11, Hauptschaltung_LED_Anzeige_1_led_6_2,
       Hauptschaltung_LED_Anzeige_1_led_6_3, Hauptschaltung_LED_Anzeige_1_led_6_4,
       Hauptschaltung_LED_Anzeige_1_led_6_5, Hauptschaltung_LED_Anzeige_1_led_6_6,
       Hauptschaltung_LED_Anzeige_1_led_6_7, Hauptschaltung_LED_Anzeige_1_led_6_8,
       Hauptschaltung_LED_Anzeige_1_led_6_9, Hauptschaltung_LED_Anzeige_1_led_6_10,
       Hauptschaltung_LED_Anzeige_1_led_6_11, Hauptschaltung_LED_Anzeige_1_led_7_2,
       Hauptschaltung_LED_Anzeige_1_led_7_4, Hauptschaltung_LED_Anzeige_1_led_7_5,
       Hauptschaltung_LED_Anzeige_1_led_7_6, Hauptschaltung_LED_Anzeige_1_led_7_7,
       Hauptschaltung_LED_Anzeige_1_led_7_9, Hauptschaltung_LED_Anzeige_1_led_7_10,
       Hauptschaltung_LED_Anzeige_1_led_7_11, Hauptschaltung_LED_Anzeige_1_led_8_2,
       Hauptschaltung_LED_Anzeige_1_led_8_3, Hauptschaltung_LED_Anzeige_1_led_8_5,
       Hauptschaltung_LED_Anzeige_1_led_8_6, Hauptschaltung_LED_Anzeige_1_led_8_7,
       Hauptschaltung_LED_Anzeige_1_led_8_8, Hauptschaltung_LED_Anzeige_1_led_8_9,
       Hauptschaltung_LED_Anzeige_1_led_8_10, Hauptschaltung_LED_Anzeige_1_led_8_11,
       Hauptschaltung_LED_Anzeige_1_led_rahmen_rest_wecker;

  _7_Segment_Display L (
    .g(hauptschaltung_7seg_anzeige_1_seg_1g), .f(hauptschaltung_7seg_anzeige_1_seg_1f),
    .a(hauptschaltung_7seg_anzeige_1_seg_1a), .b(hauptschaltung_7seg_anzeige_1_seg_1b),
    .e(hauptschaltung_7seg_anzeige_1_seg_1e), .d(hauptschaltung_7seg_anzeige_1_seg_1d),
    .c(hauptschaltung_7seg_anzeige_1_seg_1c));  // open: dp
  _7_Segment_Display LM (
    .g(hauptschaltung_7seg_anzeige_1_seg_2g), .f(hauptschaltung_7seg_anzeige_1_seg_2f),
    .a(hauptschaltung_7seg_anzeige_1_seg_2a), .b(hauptschaltung_7seg_anzeige_1_seg_2b),
    .e(hauptschaltung_7seg_anzeige_1_seg_2e), .d(hauptschaltung_7seg_anzeige_1_seg_2d),
    .c(hauptschaltung_7seg_anzeige_1_seg_2c));  // open: dp
  _7_Segment_Display R (
    .g(hauptschaltung_7seg_anzeige_1_seg_4g), .f(hauptschaltung_7seg_anzeige_1_seg_4f),
    .a(hauptschaltung_7seg_anzeige_1_seg_4a), .b(hauptschaltung_7seg_anzeige_1_seg_4b),
    .e(hauptschaltung_7seg_anzeige_1_seg_4e), .d(hauptschaltung_7seg_anzeige_1_seg_4d),
    .c(hauptschaltung_7seg_anzeige_1_seg_4c));  // open: dp
  _7_Segment_Display RM (
    .g(hauptschaltung_7seg_anzeige_1_seg_3g), .f(hauptschaltung_7seg_anzeige_1_seg_3f),
    .a(hauptschaltung_7seg_anzeige_1_seg_3a), .b(hauptschaltung_7seg_anzeige_1_seg_3b),
    .e(hauptschaltung_7seg_anzeige_1_seg_3e), .d(hauptschaltung_7seg_anzeige_1_seg_3d),
    .c(hauptschaltung_7seg_anzeige_1_seg_3c));  // open: dp
  Hauptschaltung_7Seg_Anzeige hauptschaltung_7seg_anzeige_1 (
    .Seg_1B(hauptschaltung_7seg_anzeige_1_seg_1b), .Seg_2A(hauptschaltung_7seg_anzeige_1_seg_2a),
    .Seg_1E(hauptschaltung_7seg_anzeige_1_seg_1e), .Seg_1D(hauptschaltung_7seg_anzeige_1_seg_1d),
    .Seg_1F(hauptschaltung_7seg_anzeige_1_seg_1f), .Seg_2C(hauptschaltung_7seg_anzeige_1_seg_2c),
    .Taste_Gecko_Min_Sek(in_2), .Seg_1G(hauptschaltung_7seg_anzeige_1_seg_1g),
    .Seg_1A(hauptschaltung_7seg_anzeige_1_seg_1a), .Seg_1C(hauptschaltung_7seg_anzeige_1_seg_1c),
    .Schalter_Gecko_Wecker_Stellem(in_5), .Takt_Wecker_Stellen(in_1), .Taste_Gecko_Jahr(in_4),
    .Taste_Gecko_Tag_Mon(in_3), .Seg_2D(hauptschaltung_7seg_anzeige_1_seg_2d),
    .Schalter_Gecko_Wecker_Ein_Aus(in_6), .Seg_2F(hauptschaltung_7seg_anzeige_1_seg_2f),
    .Seg_2G(hauptschaltung_7seg_anzeige_1_seg_2g), .Seg_2B(hauptschaltung_7seg_anzeige_1_seg_2b),
    .Seg_2E(hauptschaltung_7seg_anzeige_1_seg_2e), .Seg_3A(hauptschaltung_7seg_anzeige_1_seg_3a),
    .Seg_3B(hauptschaltung_7seg_anzeige_1_seg_3b), .Seg_3C(hauptschaltung_7seg_anzeige_1_seg_3c),
    .Seg_3D(hauptschaltung_7seg_anzeige_1_seg_3d), .Seg_3E(hauptschaltung_7seg_anzeige_1_seg_3e),
    .Seg_3F(hauptschaltung_7seg_anzeige_1_seg_3f), .Seg_3G(hauptschaltung_7seg_anzeige_1_seg_3g),
    .Seg_4A(hauptschaltung_7seg_anzeige_1_seg_4a), .Seg_4B(hauptschaltung_7seg_anzeige_1_seg_4b),
    .Seg_4C(hauptschaltung_7seg_anzeige_1_seg_4c), .Seg_4D(hauptschaltung_7seg_anzeige_1_seg_4d),
    .Seg_4E(hauptschaltung_7seg_anzeige_1_seg_4e), .Seg_4F(hauptschaltung_7seg_anzeige_1_seg_4f),
    .Seg_4G(hauptschaltung_7seg_anzeige_1_seg_4g),
    .Weckerfunktion_zu_LED(hauptschaltung_7seg_anzeige_1_weckerfunktion_zu_led),
    .Min_sek_zu_LED(hauptschaltung_7seg_anzeige_1_min_sek_zu_led),
    .Tag_Mon_zu_LED(hauptschaltung_7seg_anzeige_1_tag_mon_zu_led),
    .Jahr_zu_LED(hauptschaltung_7seg_anzeige_1_jahr_zu_led), .Stundenbits(in_7), .Wecker_Stundenbits(in_8),
    .Minutenbits(in_9), .Wecker_Minutenbits(in_10), .Sekundenbits(in_11), .Jahrbits(in_14), .Tagbits(in_12),
    .Monatbits(in_13));  // open: Reset_Wecker_Seg1, Reset_Wecker_Seg3_4, Reset_Wecker_Seg2
  LED led_1 (.in(Hauptschaltung_LED_Anzeige_1_led_rahmen_rest_wecker));
  LED led_2 (.in(Hauptschaltung_LED_Anzeige_1_led_rahmen_rest_wecker));
  LED led_3 (.in(Hauptschaltung_LED_Anzeige_1_led_rahmen_rest_wecker));
  LED led_4 (.in(Hauptschaltung_LED_Anzeige_1_led_rahmen_rest_wecker));
  LED led_5 (.in(Hauptschaltung_LED_Anzeige_1_led_rahmen_rest_wecker));
  LED led_6 (.in(Hauptschaltung_LED_Anzeige_1_led_rahmen_rest_wecker));
  LED led_7 (.in(Hauptschaltung_LED_Anzeige_1_led_rahmen_rest_wecker));
  LED led_8 (.in(Hauptschaltung_LED_Anzeige_1_led_rahmen_rest_wecker));
  LED led_9 (.in(Hauptschaltung_LED_Anzeige_1_led_rahmen_rest_wecker));
  LED led_10 (.in(Hauptschaltung_LED_Anzeige_1_led_rahmen_rest_wecker));
  LED led_11 (.in(Hauptschaltung_LED_Anzeige_1_led_rahmen_rest_wecker));
  LED led_12 (.in(Hauptschaltung_LED_Anzeige_1_led_rahmen_rest_wecker));
  LED led_13 (.in(Hauptschaltung_LED_Anzeige_1_led_rahmen_rest_wecker));
  LED led_14 (.in(Hauptschaltung_LED_Anzeige_1_led_rahmen_rest_wecker));
  LED led_15 (.in(Hauptschaltung_LED_Anzeige_1_led_3_2));
  LED led_16 (.in(Hauptschaltung_LED_Anzeige_1_led_3_3));
  LED led_17 (.in(Hauptschaltung_LED_Anzeige_1_led_4_2));
  LED led_18 (.in(Hauptschaltung_LED_Anzeige_1_led_rahmen_rest_wecker));
  LED led_19 (.in(Hauptschaltung_LED_Anzeige_1_led_5_3));
  LED led_20 (.in(Hauptschaltung_LED_Anzeige_1_led_5_2));
  LED led_21 (.in(Hauptschaltung_LED_Anzeige_1_led_6_3));
  LED led_22 (.in(Hauptschaltung_LED_Anzeige_1_led_6_2));
  LED led_23 (.in(Hauptschaltung_LED_Anzeige_1_led_7_2));
  LED led_24 (.in(Hauptschaltung_LED_Anzeige_1_led_rahmen_rest_wecker));
  LED led_25 (.in(Hauptschaltung_LED_Anzeige_1_led_8_3));
  LED led_26 (.in(Hauptschaltung_LED_Anzeige_1_led_8_2));
  LED led_27 (.in(Hauptschaltung_LED_Anzeige_1_led_rahmen_rest_wecker));
  LED led_28 (.in(Hauptschaltung_LED_Anzeige_1_led_rahmen_rest_wecker));
  LED led_29 (.in(Hauptschaltung_LED_Anzeige_1_led_rahmen_rest_wecker));
  LED led_30 (.in(Hauptschaltung_LED_Anzeige_1_led_rahmen_rest_wecker));
  LED led_31 (.in(Hauptschaltung_LED_Anzeige_1_led_rahmen_rest_wecker));
  LED led_32 (.in(Hauptschaltung_LED_Anzeige_1_led_rahmen_rest_wecker));
  LED led_33 (.in(Hauptschaltung_LED_Anzeige_1_led_rahmen_rest_wecker));
  LED led_34 (.in(Hauptschaltung_LED_Anzeige_1_led_rahmen_rest_wecker));
  LED led_35 (.in(Hauptschaltung_LED_Anzeige_1_led_rahmen_rest_wecker));
  LED led_36 (.in(Hauptschaltung_LED_Anzeige_1_led_rahmen_rest_wecker));
  LED led_37 (.in(Hauptschaltung_LED_Anzeige_1_led_4_4));
  LED led_38 (.in(Hauptschaltung_LED_Anzeige_1_led_rahmen_rest_wecker));
  LED led_39 (.in(Hauptschaltung_LED_Anzeige_1_led_5_5));
  LED led_40 (.in(Hauptschaltung_LED_Anzeige_1_led_5_4));
  LED led_41 (.in(Hauptschaltung_LED_Anzeige_1_led_6_5));
  LED led_42 (.in(Hauptschaltung_LED_Anzeige_1_led_6_4));
  LED led_43 (.in(Hauptschaltung_LED_Anzeige_1_led_7_5));
  LED led_44 (.in(Hauptschaltung_LED_Anzeige_1_led_7_4));
  LED led_45 (.in(Hauptschaltung_LED_Anzeige_1_led_8_5));
  LED led_46 (.in(Hauptschaltung_LED_Anzeige_1_led_rahmen_rest_wecker));
  LED led_47 (.in(Hauptschaltung_LED_Anzeige_1_led_rahmen_rest_wecker));
  LED led_48 (.in(Hauptschaltung_LED_Anzeige_1_led_rahmen_rest_wecker));
  LED led_49 (.in(Hauptschaltung_LED_Anzeige_1_led_rahmen_rest_wecker));
  LED led_50 (.in(Hauptschaltung_LED_Anzeige_1_led_rahmen_rest_wecker));
  LED led_51 (.in(Hauptschaltung_LED_Anzeige_1_led_rahmen_rest_wecker));
  LED led_52 (.in(Hauptschaltung_LED_Anzeige_1_led_rahmen_rest_wecker));
  LED led_53 (.in(Hauptschaltung_LED_Anzeige_1_led_rahmen_rest_wecker));
  LED led_54 (.in(Hauptschaltung_LED_Anzeige_1_led_rahmen_rest_wecker));
  LED led_55 (.in(Hauptschaltung_LED_Anzeige_1_led_rahmen_rest_wecker));
  LED led_56 (.in(Hauptschaltung_LED_Anzeige_1_led_3_7));
  LED led_57 (.in(Hauptschaltung_LED_Anzeige_1_led_rahmen_rest_wecker));
  LED led_58 (.in(Hauptschaltung_LED_Anzeige_1_led_4_7));
  LED led_59 (.in(Hauptschaltung_LED_Anzeige_1_led_5_7));
  LED led_60 (.in(Hauptschaltung_LED_Anzeige_1_led_5_6));
  LED led_61 (.in(Hauptschaltung_LED_Anzeige_1_led_6_6));
  LED led_62 (.in(Hauptschaltung_LED_Anzeige_1_led_6_7));
  LED led_63 (.in(Hauptschaltung_LED_Anzeige_1_led_7_6));
  LED led_64 (.in(Hauptschaltung_LED_Anzeige_1_led_7_7));
  LED led_65 (.in(Hauptschaltung_LED_Anzeige_1_led_8_7));
  LED led_66 (.in(Hauptschaltung_LED_Anzeige_1_led_8_6));
  LED led_67 (.in(Hauptschaltung_LED_Anzeige_1_led_rahmen_rest_wecker));
  LED led_68 (.in(Hauptschaltung_LED_Anzeige_1_led_rahmen_rest_wecker));
  LED led_69 (.in(Hauptschaltung_LED_Anzeige_1_led_rahmen_rest_wecker));
  LED led_70 (.in(Hauptschaltung_LED_Anzeige_1_led_rahmen_rest_wecker));
  LED led_71 (.in(Hauptschaltung_LED_Anzeige_1_led_rahmen_rest_wecker));
  LED led_72 (.in(Hauptschaltung_LED_Anzeige_1_led_rahmen_rest_wecker));
  LED led_73 (.in(Hauptschaltung_LED_Anzeige_1_led_rahmen_rest_wecker));
  LED led_74 (.in(Hauptschaltung_LED_Anzeige_1_led_rahmen_rest_wecker));
  LED led_75 (.in(Hauptschaltung_LED_Anzeige_1_led_rahmen_rest_wecker));
  LED led_76 (.in(Hauptschaltung_LED_Anzeige_1_led_rahmen_rest_wecker));
  LED led_77 (.in(Hauptschaltung_LED_Anzeige_1_led_4_9));
  LED led_78 (.in(Hauptschaltung_LED_Anzeige_1_led_4_8));
  LED led_79 (.in(Hauptschaltung_LED_Anzeige_1_led_5_9));
  LED led_80 (.in(Hauptschaltung_LED_Anzeige_1_led_5_8));
  LED led_81 (.in(Hauptschaltung_LED_Anzeige_1_led_6_9));
  LED led_82 (.in(Hauptschaltung_LED_Anzeige_1_led_6_8));
  LED led_83 (.in(Hauptschaltung_LED_Anzeige_1_led_rahmen_rest_wecker));
  LED led_84 (.in(Hauptschaltung_LED_Anzeige_1_led_7_9));
  LED led_85 (.in(Hauptschaltung_LED_Anzeige_1_led_8_8));
  LED led_86 (.in(Hauptschaltung_LED_Anzeige_1_led_8_9));
  LED led_87 (.in(Hauptschaltung_LED_Anzeige_1_led_rahmen_rest_wecker));
  LED led_88 (.in(Hauptschaltung_LED_Anzeige_1_led_rahmen_rest_wecker));
  LED led_89 (.in(Hauptschaltung_LED_Anzeige_1_led_rahmen_rest_wecker));
  LED led_90 (.in(Hauptschaltung_LED_Anzeige_1_led_rahmen_rest_wecker));
  LED led_91 (.in(Hauptschaltung_LED_Anzeige_1_led_rahmen_rest_wecker));
  LED led_92 (.in(Hauptschaltung_LED_Anzeige_1_led_rahmen_rest_wecker));
  LED led_93 (.in(Hauptschaltung_LED_Anzeige_1_led_rahmen_rest_wecker));
  LED led_94 (.in(Hauptschaltung_LED_Anzeige_1_led_rahmen_rest_wecker));
  LED led_95 (.in(Hauptschaltung_LED_Anzeige_1_led_3_11));
  LED led_96 (.in(Hauptschaltung_LED_Anzeige_1_led_rahmen_rest_wecker));
  LED led_97 (.in(Hauptschaltung_LED_Anzeige_1_led_4_11));
  LED led_98 (.in(Hauptschaltung_LED_Anzeige_1_led_4_10));
  LED led_99 (.in(Hauptschaltung_LED_Anzeige_1_led_5_10));
  LED led_100 (.in(Hauptschaltung_LED_Anzeige_1_led_5_11));
  LED led_101 (.in(Hauptschaltung_LED_Anzeige_1_led_6_10));
  LED led_102 (.in(Hauptschaltung_LED_Anzeige_1_led_6_11));
  LED led_103 (.in(Hauptschaltung_LED_Anzeige_1_led_7_11));
  LED led_104 (.in(Hauptschaltung_LED_Anzeige_1_led_7_10));
  LED led_105 (.in(Hauptschaltung_LED_Anzeige_1_led_8_11));
  LED led_106 (.in(Hauptschaltung_LED_Anzeige_1_led_8_10));
  LED led_107 (.in(Hauptschaltung_LED_Anzeige_1_led_rahmen_rest_wecker));
  LED led_108 (.in(Hauptschaltung_LED_Anzeige_1_led_rahmen_rest_wecker));
  LED led_109 (.in(Hauptschaltung_LED_Anzeige_1_led_rahmen_rest_wecker));
  LED led_110 (.in(Hauptschaltung_LED_Anzeige_1_led_rahmen_rest_wecker));
  Hauptschaltung_LED_Anzeige Hauptschaltung_LED_Anzeige_1 (
    .LED_6_11(Hauptschaltung_LED_Anzeige_1_led_6_11), .LED_6_10(Hauptschaltung_LED_Anzeige_1_led_6_10),
    .LED_6_9(Hauptschaltung_LED_Anzeige_1_led_6_9), .LED_6_8(Hauptschaltung_LED_Anzeige_1_led_6_8),
    .LED_6_7(Hauptschaltung_LED_Anzeige_1_led_6_7), .LED_6_6(Hauptschaltung_LED_Anzeige_1_led_6_6),
    .LED_6_5(Hauptschaltung_LED_Anzeige_1_led_6_5), .LED_6_4(Hauptschaltung_LED_Anzeige_1_led_6_4),
    .LED_6_3(Hauptschaltung_LED_Anzeige_1_led_6_3), .LED_6_2(Hauptschaltung_LED_Anzeige_1_led_6_2),
    .LED_5_11(Hauptschaltung_LED_Anzeige_1_led_5_11), .LED_5_10(Hauptschaltung_LED_Anzeige_1_led_5_10),
    .LED_5_9(Hauptschaltung_LED_Anzeige_1_led_5_9), .LED_5_8(Hauptschaltung_LED_Anzeige_1_led_5_8),
    .LED_5_7(Hauptschaltung_LED_Anzeige_1_led_5_7), .LED_5_6(Hauptschaltung_LED_Anzeige_1_led_5_6),
    .LED_5_5(Hauptschaltung_LED_Anzeige_1_led_5_5), .LED_5_4(Hauptschaltung_LED_Anzeige_1_led_5_4),
    .LED_5_3(Hauptschaltung_LED_Anzeige_1_led_5_3), .LED_5_2(Hauptschaltung_LED_Anzeige_1_led_5_2),
    .LED_4_11(Hauptschaltung_LED_Anzeige_1_led_4_11), .LED_4_10(Hauptschaltung_LED_Anzeige_1_led_4_10),
    .LED_4_9(Hauptschaltung_LED_Anzeige_1_led_4_9), .LED_4_8(Hauptschaltung_LED_Anzeige_1_led_4_8),
    .LED_4_7(Hauptschaltung_LED_Anzeige_1_led_4_7), .LED_4_4(Hauptschaltung_LED_Anzeige_1_led_4_4),
    .LED_4_2(Hauptschaltung_LED_Anzeige_1_led_4_2), .LED_3_11(Hauptschaltung_LED_Anzeige_1_led_3_11),
    .LED_3_7(Hauptschaltung_LED_Anzeige_1_led_3_7), .LED_3_3(Hauptschaltung_LED_Anzeige_1_led_3_3),
    .LED_3_2(Hauptschaltung_LED_Anzeige_1_led_3_2),
    .LED_Rahmen_Rest_Wecker(Hauptschaltung_LED_Anzeige_1_led_rahmen_rest_wecker),
    .Eingangstaste_Jahr(hauptschaltung_7seg_anzeige_1_jahr_zu_led),
    .Eingangstaste_Tag_Monat(hauptschaltung_7seg_anzeige_1_tag_mon_zu_led),
    .Eingangstaste_Min_Sek(hauptschaltung_7seg_anzeige_1_min_sek_zu_led),
    .Weckfunktion(hauptschaltung_7seg_anzeige_1_weckerfunktion_zu_led), .Input_1(in_1),
    .LED_7_2(Hauptschaltung_LED_Anzeige_1_led_7_2), .LED_7_4(Hauptschaltung_LED_Anzeige_1_led_7_4),
    .LED_7_5(Hauptschaltung_LED_Anzeige_1_led_7_5), .LED_7_6(Hauptschaltung_LED_Anzeige_1_led_7_6),
    .LED_7_7(Hauptschaltung_LED_Anzeige_1_led_7_7), .LED_7_9(Hauptschaltung_LED_Anzeige_1_led_7_9),
    .LED_7_10(Hauptschaltung_LED_Anzeige_1_led_7_10), .LED_7_11(Hauptschaltung_LED_Anzeige_1_led_7_11),
    .LED_8_2(Hauptschaltung_LED_Anzeige_1_led_8_2), .LED_8_3(Hauptschaltung_LED_Anzeige_1_led_8_3),
    .LED_8_5(Hauptschaltung_LED_Anzeige_1_led_8_5), .LED_8_6(Hauptschaltung_LED_Anzeige_1_led_8_6),
    .LED_8_7(Hauptschaltung_LED_Anzeige_1_led_8_7), .LED_8_8(Hauptschaltung_LED_Anzeige_1_led_8_8),
    .LED_8_9(Hauptschaltung_LED_Anzeige_1_led_8_9), .LED_8_10(Hauptschaltung_LED_Anzeige_1_led_8_10),
    .LED_8_11(Hauptschaltung_LED_Anzeige_1_led_8_11));
  LED led_111 (.in(Hauptschaltung_LED_Anzeige_1_led_rahmen_rest_wecker));
  LED led_112 (.in(Hauptschaltung_LED_Anzeige_1_led_rahmen_rest_wecker));
  LED led_113 (.in(Hauptschaltung_LED_Anzeige_1_led_rahmen_rest_wecker));
  LED led_114 (.in(Hauptschaltung_LED_Anzeige_1_led_rahmen_rest_wecker));
  LED led_115 (.in(Hauptschaltung_LED_Anzeige_1_led_rahmen_rest_wecker));
  LED led_116 (.in(Hauptschaltung_LED_Anzeige_1_led_rahmen_rest_wecker));
  LED led_117 (.in(Hauptschaltung_LED_Anzeige_1_led_rahmen_rest_wecker));
  LED led_118 (.in(Hauptschaltung_LED_Anzeige_1_led_rahmen_rest_wecker));
  LED led_119 (.in(Hauptschaltung_LED_Anzeige_1_led_rahmen_rest_wecker));
  LED led_120 (.in(Hauptschaltung_LED_Anzeige_1_led_rahmen_rest_wecker));
endmodule

module h_und_m (
  input  Taste_min_sek,
  input  Taste_tag_mon,
  input  Taste_jahr,
  output LED_3_2,
  output LED_4_2,
  output LED_5_2,
  output LED_5_7,
  output LED_5_8,
  output LED_5_9,
  output LED_5_10,
  output LED_5_11,
  output LED_6_2,
  output LED_6_3,
  output LED_6_4,
  output LED_6_5,
  output LED_6_7,
  output LED_6_9,
  output LED_6_11,
  output LED_7_2,
  output LED_7_5,
  output LED_7_7,
  output LED_7_9,
  output LED_7_11,
  output LED_8_2,
  output LED_8_5,
  output LED_8_7,
  output LED_8_11
);

  and and_1 (LED_3_2, ~Taste_min_sek, ~Taste_tag_mon, ~Taste_jahr);  // AND_Gate

  assign LED_4_2 = LED_3_2;
  assign LED_5_2 = LED_3_2;
  assign LED_5_7 = LED_3_2;
  assign LED_5_8 = LED_3_2;
  assign LED_5_9 = LED_3_2;
  assign LED_5_10 = LED_3_2;
  assign LED_5_11 = LED_3_2;
  assign LED_6_2 = LED_3_2;
  assign LED_6_3 = LED_3_2;
  assign LED_6_4 = LED_3_2;
  assign LED_6_5 = LED_3_2;
  assign LED_6_7 = LED_3_2;
  assign LED_6_9 = LED_3_2;
  assign LED_6_11 = LED_3_2;
  assign LED_7_2 = LED_3_2;
  assign LED_7_5 = LED_3_2;
  assign LED_7_7 = LED_3_2;
  assign LED_7_9 = LED_3_2;
  assign LED_7_11 = LED_3_2;
  assign LED_8_2 = LED_3_2;
  assign LED_8_5 = LED_3_2;
  assign LED_8_7 = LED_3_2;
  assign LED_8_11 = LED_3_2;
endmodule

module m_und_s (
  input  Taste_min_sek,
  output LED_4_8,
  output LED_4_9,
  output LED_4_10,
  output LED_5_2,
  output LED_5_3,
  output LED_5_4,
  output LED_5_5,
  output LED_5_6,
  output LED_5_8,
  output LED_6_2,
  output LED_6_4,
  output LED_6_6,
  output LED_6_8,
  output LED_6_9,
  output LED_6_10,
  output LED_7_2,
  output LED_7_4,
  output LED_7_6,
  output LED_7_10,
  output LED_8_2,
  output LED_8_6,
  output LED_8_8,
  output LED_8_9,
  output LED_8_10
);


  assign LED_4_8 = Taste_min_sek;
  assign LED_4_9 = Taste_min_sek;
  assign LED_4_10 = Taste_min_sek;
  assign LED_5_2 = Taste_min_sek;
  assign LED_5_3 = Taste_min_sek;
  assign LED_5_4 = Taste_min_sek;
  assign LED_5_5 = Taste_min_sek;
  assign LED_5_6 = Taste_min_sek;
  assign LED_5_8 = Taste_min_sek;
  assign LED_6_2 = Taste_min_sek;
  assign LED_6_4 = Taste_min_sek;
  assign LED_6_6 = Taste_min_sek;
  assign LED_6_8 = Taste_min_sek;
  assign LED_6_9 = Taste_min_sek;
  assign LED_6_10 = Taste_min_sek;
  assign LED_7_2 = Taste_min_sek;
  assign LED_7_4 = Taste_min_sek;
  assign LED_7_6 = Taste_min_sek;
  assign LED_7_10 = Taste_min_sek;
  assign LED_8_2 = Taste_min_sek;
  assign LED_8_6 = Taste_min_sek;
  assign LED_8_8 = Taste_min_sek;
  assign LED_8_9 = Taste_min_sek;
  assign LED_8_10 = Taste_min_sek;
endmodule

module D_und_M (
  input  Taste_Tag_Monat,
  output LED_3_2,
  output LED_3_3,
  output LED_3_7,
  output LED_3_11,
  output LED_4_2,
  output LED_4_4,
  output LED_4_7,
  output LED_4_8,
  output LED_4_10,
  output LED_4_11,
  output LED_5_2,
  output LED_5_5,
  output LED_5_7,
  output LED_5_9,
  output LED_5_11,
  output LED_6_2,
  output LED_6_5,
  output LED_6_7,
  output LED_6_11,
  output LED_7_2,
  output LED_7_4,
  output LED_7_7,
  output LED_7_11,
  output LED_8_2,
  output LED_8_3,
  output LED_8_7,
  output LED_8_11
);


  assign LED_3_2 = Taste_Tag_Monat;
  assign LED_3_3 = Taste_Tag_Monat;
  assign LED_3_7 = Taste_Tag_Monat;
  assign LED_3_11 = Taste_Tag_Monat;
  assign LED_4_2 = Taste_Tag_Monat;
  assign LED_4_4 = Taste_Tag_Monat;
  assign LED_4_7 = Taste_Tag_Monat;
  assign LED_4_8 = Taste_Tag_Monat;
  assign LED_4_10 = Taste_Tag_Monat;
  assign LED_4_11 = Taste_Tag_Monat;
  assign LED_5_2 = Taste_Tag_Monat;
  assign LED_5_5 = Taste_Tag_Monat;
  assign LED_5_7 = Taste_Tag_Monat;
  assign LED_5_9 = Taste_Tag_Monat;
  assign LED_5_11 = Taste_Tag_Monat;
  assign LED_6_2 = Taste_Tag_Monat;
  assign LED_6_5 = Taste_Tag_Monat;
  assign LED_6_7 = Taste_Tag_Monat;
  assign LED_6_11 = Taste_Tag_Monat;
  assign LED_7_2 = Taste_Tag_Monat;
  assign LED_7_4 = Taste_Tag_Monat;
  assign LED_7_7 = Taste_Tag_Monat;
  assign LED_7_11 = Taste_Tag_Monat;
  assign LED_8_2 = Taste_Tag_Monat;
  assign LED_8_3 = Taste_Tag_Monat;
  assign LED_8_7 = Taste_Tag_Monat;
  assign LED_8_11 = Taste_Tag_Monat;
endmodule

module Y (
  input  Taste_Jahr,
  output LED_3_7,
  output LED_3_11,
  output LED_4_7,
  output LED_4_11,
  output LED_5_8,
  output LED_5_10,
  output LED_6_9,
  output LED_7_9,
  output LED_8_9
);


  assign LED_3_7 = Taste_Jahr;
  assign LED_3_11 = Taste_Jahr;
  assign LED_4_7 = Taste_Jahr;
  assign LED_4_11 = Taste_Jahr;
  assign LED_5_8 = Taste_Jahr;
  assign LED_5_10 = Taste_Jahr;
  assign LED_6_9 = Taste_Jahr;
  assign LED_7_9 = Taste_Jahr;
  assign LED_8_9 = Taste_Jahr;
endmodule
